// Logisim project tennis_cdmtest.circ as structural Verilog: 9 circuits, main circuit main
module main (
  input  [7:0] in_1,
  input  [7:0] in_2,
  input  [7:0] speed,
  input  reset
);

  wire clock_1_out;
  wire [4:0] joystick, joystick_1_y, kinematic_controller_1_ballx_2, kinematic_controller_1_bally_2, robot,
       videosub_1_ballx, videosub_1_bally, videosub_1_chipid, videosub_1_leftbat, videosub_1_rightbat,
       videosub_2_ballx, videosub_2_bally, videosub_2_chipid, videosub_2_leftbat, videosub_2_rightbat,
       videosub_3_ballx, videosub_3_bally, videosub_3_chipid, videosub_3_leftbat, videosub_3_rightbat;
  wire [31:0] videosub_1_out_6, videosub_1_out_7, videosub_1_out_8, videosub_1_out_9, videosub_1_out_10,
       videosub_1_out_11, videosub_1_out_12, videosub_1_out_13, videosub_2_out_6, videosub_2_out_7,
       videosub_2_out_8, videosub_2_out_9, videosub_2_out_10, videosub_2_out_11, videosub_2_out_12,
       videosub_2_out_13, videosub_3_out_6, videosub_3_out_7, videosub_3_out_8, videosub_3_out_9,
       videosub_3_out_10, videosub_3_out_11, videosub_3_out_12, videosub_3_out_13, videosub_4_out_6,
       videosub_4_out_7, videosub_4_out_8, videosub_4_out_9, videosub_4_out_10, videosub_4_out_11,
       videosub_4_out_12, videosub_4_out_13;

  Joystick #(.bits(5)) joystick_1 (.y(joystick_1_y));  // open: x
  assign joystick = ~joystick_1_y;  // NOT_Gate not_1, 5 bits wide
  Kinematic_controller kinematic_controller_1 (
    .BallX(in_1), .BallY(in_2), .Vxy(speed), .reset(reset), .BallX_2(kinematic_controller_1_ballx_2),
    .BallY_2(kinematic_controller_1_bally_2), .clock(clock_1_out), .LeftBat(joystick), .out_7(robot));
  Clock clock_1 (.out(clock_1_out));
  _7_Segment_Display u_7_segment_display_1 ();  // open: g, f, a, b, e, d, c, dp
  _7_Segment_Display u_7_segment_display_2 ();  // open: g, f, a, b, e, d, c, dp
  videoSub videosub_1 (
    .out_6(videosub_1_out_6), .out_7(videosub_1_out_7), .out_8(videosub_1_out_8), .out_9(videosub_1_out_9),
    .out_10(videosub_1_out_10), .out_11(videosub_1_out_11), .out_12(videosub_1_out_12),
    .out_13(videosub_1_out_13), .in_1(kinematic_controller_1_ballx_2), .in_2(kinematic_controller_1_bally_2),
    .in_3(robot), .in_4(joystick), .in_5({5{1'b0}}), .BallX(videosub_1_ballx), .BallY(videosub_1_bally),
    .rightBat(videosub_1_rightbat), .leftBat(videosub_1_leftbat), .chipID(videosub_1_chipid));
  DotMatrix #(.matrixcols(32), .matrixrows(32)) dotmatrix_1 (
    .col0(videosub_1_out_6), .col1(videosub_1_out_7), .col2(videosub_1_out_8), .col3(videosub_1_out_9),
    .col4(videosub_1_out_10), .col5(videosub_1_out_11), .col6(videosub_1_out_12), .col7(videosub_1_out_13),
    .col8(videosub_2_out_6), .col9(videosub_2_out_7), .col10(videosub_2_out_8), .col11(videosub_2_out_9),
    .col12(videosub_2_out_10), .col13(videosub_2_out_11), .col14(videosub_2_out_12),
    .col15(videosub_2_out_13), .col16(videosub_3_out_6), .col17(videosub_3_out_7), .col18(videosub_3_out_8),
    .col19(videosub_3_out_9), .col20(videosub_3_out_10), .col21(videosub_3_out_11),
    .col22(videosub_3_out_12), .col23(videosub_3_out_13), .col24(videosub_4_out_6), .col25(videosub_4_out_7),
    .col26(videosub_4_out_8), .col27(videosub_4_out_9), .col28(videosub_4_out_10), .col29(videosub_4_out_11),
    .col30(videosub_4_out_12), .col31(videosub_4_out_13));
  videoSub videosub_2 (
    .out_6(videosub_2_out_6), .out_7(videosub_2_out_7), .out_8(videosub_2_out_8), .out_9(videosub_2_out_9),
    .out_10(videosub_2_out_10), .out_11(videosub_2_out_11), .out_12(videosub_2_out_12),
    .out_13(videosub_2_out_13), .in_1(videosub_1_ballx), .in_2(videosub_1_bally), .in_3(videosub_1_rightbat),
    .in_4(videosub_1_leftbat), .in_5(videosub_1_chipid), .BallX(videosub_2_ballx), .BallY(videosub_2_bally),
    .rightBat(videosub_2_rightbat), .leftBat(videosub_2_leftbat), .chipID(videosub_2_chipid));
  videoSub videosub_3 (
    .out_6(videosub_3_out_6), .out_7(videosub_3_out_7), .out_8(videosub_3_out_8), .out_9(videosub_3_out_9),
    .out_10(videosub_3_out_10), .out_11(videosub_3_out_11), .out_12(videosub_3_out_12),
    .out_13(videosub_3_out_13), .in_1(videosub_2_ballx), .in_2(videosub_2_bally), .in_3(videosub_2_rightbat),
    .in_4(videosub_2_leftbat), .in_5(videosub_2_chipid), .BallX(videosub_3_ballx), .BallY(videosub_3_bally),
    .rightBat(videosub_3_rightbat), .leftBat(videosub_3_leftbat), .chipID(videosub_3_chipid));
  videoSub videosub_4 (
    .out_6(videosub_4_out_6), .out_7(videosub_4_out_7), .out_8(videosub_4_out_8), .out_9(videosub_4_out_9),
    .out_10(videosub_4_out_10), .out_11(videosub_4_out_11), .out_12(videosub_4_out_12),
    .out_13(videosub_4_out_13), .in_1(videosub_3_ballx), .in_2(videosub_3_bally), .in_3(videosub_3_rightbat),
    .in_4(videosub_3_leftbat), .in_5(videosub_3_chipid));  // open: BallX, BallY, rightBat, leftBat, chipID
  _7_Segment_Display u_7_segment_display_3 ();  // open: g, f, a, b, e, d, c, dp
  _7_Segment_Display u_7_segment_display_4 ();  // open: g, f, a, b, e, d, c, dp

  // Other names for the same wires on the sheet: X[7:0] = in_1; Y[7:0] = in_2
endmodule

module videochip (
  input  [4:0] BallX,
  input  [4:0] BallY,
  input  [4:0] rightBat,
  input  [4:0] leftBat,
  input  [4:0] chipID,
  output [31:0] out_6,
  output [4:0] BallX_2,
  output [4:0] BallY_2,
  output [4:0] rightBat_2,
  output [4:0] leftBat_2,
  output [4:0] chipID_2
);

  wire comparator_1_eq, comparator_2_eq, comparator_3_eq;
  wire [31:0] decoder_1_out0, decoder_2_out0, decoder_3_out0, multiplexer_1_out, multiplexer_2_out,
       multiplexer_3_out, or_1_out, or_2_out, shifter_1_out, shifter_2_out, shifter_3_out, shifter_4_out;

  Adder #(.width(5)) adder_1 (.a(chipID), .b(5'b00001), .out(chipID_2));  // open: cin, cout
  Comparator #(.width(5), .mode("unsigned")) comparator_1 (
    .a(BallX), .b(chipID), .eq(comparator_1_eq));  // open: gt, lt
  Comparator #(.width(5), .mode("unsigned")) comparator_2 (
    .a(chipID), .b(5'b00011), .eq(comparator_2_eq));  // open: gt, lt
  Comparator #(.width(5), .mode("unsigned")) comparator_3 (
    .a(chipID), .b(5'b11100), .eq(comparator_3_eq));  // open: gt, lt
  // Probe on 5'b11100
  Decoder #(.select(5), .enable("false")) decoder_1 (
    .out0(decoder_1_out0[0]), .out1(decoder_1_out0[1]), .out2(decoder_1_out0[2]), .out3(decoder_1_out0[3]),
    .out4(decoder_1_out0[4]), .out5(decoder_1_out0[5]), .out6(decoder_1_out0[6]), .out7(decoder_1_out0[7]),
    .out8(decoder_1_out0[8]), .out9(decoder_1_out0[9]), .out10(decoder_1_out0[10]),
    .out11(decoder_1_out0[11]), .out12(decoder_1_out0[12]), .out13(decoder_1_out0[13]),
    .out14(decoder_1_out0[14]), .out15(decoder_1_out0[15]), .out16(decoder_1_out0[16]),
    .out17(decoder_1_out0[17]), .out18(decoder_1_out0[18]), .out19(decoder_1_out0[19]),
    .out20(decoder_1_out0[20]), .out21(decoder_1_out0[21]), .out22(decoder_1_out0[22]),
    .out23(decoder_1_out0[23]), .out24(decoder_1_out0[24]), .out25(decoder_1_out0[25]),
    .out26(decoder_1_out0[26]), .out27(decoder_1_out0[27]), .out28(decoder_1_out0[28]),
    .out29(decoder_1_out0[29]), .out30(decoder_1_out0[30]), .out31(decoder_1_out0[31]), .sel(rightBat));
  Decoder #(.select(5), .enable("false")) decoder_2 (
    .out0(decoder_2_out0[0]), .out1(decoder_2_out0[1]), .out2(decoder_2_out0[2]), .out3(decoder_2_out0[3]),
    .out4(decoder_2_out0[4]), .out5(decoder_2_out0[5]), .out6(decoder_2_out0[6]), .out7(decoder_2_out0[7]),
    .out8(decoder_2_out0[8]), .out9(decoder_2_out0[9]), .out10(decoder_2_out0[10]),
    .out11(decoder_2_out0[11]), .out12(decoder_2_out0[12]), .out13(decoder_2_out0[13]),
    .out14(decoder_2_out0[14]), .out15(decoder_2_out0[15]), .out16(decoder_2_out0[16]),
    .out17(decoder_2_out0[17]), .out18(decoder_2_out0[18]), .out19(decoder_2_out0[19]),
    .out20(decoder_2_out0[20]), .out21(decoder_2_out0[21]), .out22(decoder_2_out0[22]),
    .out23(decoder_2_out0[23]), .out24(decoder_2_out0[24]), .out25(decoder_2_out0[25]),
    .out26(decoder_2_out0[26]), .out27(decoder_2_out0[27]), .out28(decoder_2_out0[28]),
    .out29(decoder_2_out0[29]), .out30(decoder_2_out0[30]), .out31(decoder_2_out0[31]), .sel(BallY));
  Decoder #(.select(5), .enable("false")) decoder_3 (
    .out0(decoder_3_out0[0]), .out1(decoder_3_out0[1]), .out2(decoder_3_out0[2]), .out3(decoder_3_out0[3]),
    .out4(decoder_3_out0[4]), .out5(decoder_3_out0[5]), .out6(decoder_3_out0[6]), .out7(decoder_3_out0[7]),
    .out8(decoder_3_out0[8]), .out9(decoder_3_out0[9]), .out10(decoder_3_out0[10]),
    .out11(decoder_3_out0[11]), .out12(decoder_3_out0[12]), .out13(decoder_3_out0[13]),
    .out14(decoder_3_out0[14]), .out15(decoder_3_out0[15]), .out16(decoder_3_out0[16]),
    .out17(decoder_3_out0[17]), .out18(decoder_3_out0[18]), .out19(decoder_3_out0[19]),
    .out20(decoder_3_out0[20]), .out21(decoder_3_out0[21]), .out22(decoder_3_out0[22]),
    .out23(decoder_3_out0[23]), .out24(decoder_3_out0[24]), .out25(decoder_3_out0[25]),
    .out26(decoder_3_out0[26]), .out27(decoder_3_out0[27]), .out28(decoder_3_out0[28]),
    .out29(decoder_3_out0[29]), .out30(decoder_3_out0[30]), .out31(decoder_3_out0[31]), .sel(leftBat));
  Multiplexer #(.width(32), .enable("false")) multiplexer_1 (
    .in0({32{1'b0}}), .in1(decoder_2_out0), .out(multiplexer_1_out), .sel(comparator_1_eq));
  Multiplexer #(.width(32), .enable("false")) multiplexer_2 (
    .in0({32{1'b0}}), .in1(decoder_3_out0), .out(multiplexer_2_out), .sel(comparator_2_eq));
  Multiplexer #(.width(32), .enable("false")) multiplexer_3 (
    .in0({32{1'b0}}), .in1(decoder_1_out0), .out(multiplexer_3_out), .sel(comparator_3_eq));
  Shifter #(.width(32)) shifter_1 (.in(multiplexer_2_out), .\dist (5'b00001), .out(shifter_1_out));
  Shifter #(.width(32)) shifter_2 (.in(multiplexer_3_out), .\dist (5'b00001), .out(shifter_2_out));
  Shifter #(.width(32)) shifter_3 (.in(shifter_1_out), .\dist (5'b00001), .out(shifter_3_out));
  Shifter #(.width(32)) shifter_4 (.in(shifter_2_out), .\dist (5'b00001), .out(shifter_4_out));
  assign or_1_out = multiplexer_2_out | shifter_1_out | shifter_3_out;  // OR_Gate or_1, 32 bits wide
  assign or_2_out = multiplexer_3_out | shifter_2_out | shifter_4_out;  // OR_Gate or_2, 32 bits wide
  assign out_6 = multiplexer_1_out | or_1_out | or_2_out;  // OR_Gate or_3, 32 bits wide

  assign BallX_2 = BallX;
  assign BallY_2 = BallY;
  assign leftBat_2 = leftBat;
  assign rightBat_2 = rightBat;
endmodule

module Kinematic_controller (
  input  [7:0] BallX,
  input  [7:0] BallY,
  input  [7:0] Vxy,
  input  [4:0] LeftBat,
  input  clock,
  input  reset,
  output [4:0] out_7,
  output [4:0] BallX_2,
  output [4:0] BallY_2
);

  wire controlled_buffer_1_out, is_hit_the_left_1_out_4, is_hit_the_right_1_out_4, multiplexer_1_out,
       multiplexer_2_out, multiplexer_3_out, multiplexer_6_out, multiplexer_7_out, multiplexer_8_out,
       not_5_out, not_6_out, nrun_prime, reflect, reflect_t, reflectX, reflrctbtlft, rightref, run, X_C_flag,
       Y_C_flag;
  wire [2:0] controlled_buffer_4_out, controlled_buffer_5_out;
  wire [5:0] VXYTOROB;
  wire [7:0] adder_1_out, adder_2_out, BallX_POST, BallX_PRE, BallY_POST, BallY_PRE, controlled_buffer_8_out,
       controlled_buffer_9_out, controlled_buffer_10_out, controlled_buffer_11_out, counter_1_q,
       invert_v_1_out_2, invert_v_2_out_2, main_1_out_4, shifter_1_out, shifter_2_out, shifter_3_out,
       Vx_POST, Vx_PRE, Vy_POST, Vy_PRE;

  Controller_Device__CdM8_conection_main main_1 (
    .out_4(main_1_out_4), .in_1({2'b00, VXYTOROB}), .in_2(BallX_PRE), .in_3(BallY_PRE));
  Counter counter_1 (.Q(counter_1_q), .clk(controlled_buffer_1_out), .clr(reset));  // open: load, D, count, carry
  assign controlled_buffer_1_out = run ? clock : 1'bz;  // Controlled_Buffer controlled_buffer_1
  assign BallX_POST = run ? BallX : 8'bz;  // Controlled_Buffer controlled_buffer_2
  assign BallY_POST = run ? BallY : 8'bz;  // Controlled_Buffer controlled_buffer_3
  _3_bit_to_8_sign u_3_bit_to_8_sign_1 (.in_1(controlled_buffer_4_out), .out_2(Vx_POST));
  assign controlled_buffer_4_out = run ? Vxy[2:0] : 3'bz;  // Controlled_Buffer controlled_buffer_4
  assign controlled_buffer_5_out = run ? Vxy[5:3] : 3'bz;  // Controlled_Buffer controlled_buffer_5
  _3_bit_to_8_sign u_3_bit_to_8_sign_2 (.in_1(controlled_buffer_5_out), .out_2(Vy_POST));
  Comparator #(.mode("unsigned")) comparator_1 (.a(counter_1_q), .b(8'h2), .lt(run));  // open: gt, eq
  not not_1 (nrun_prime, run);
  Shifter #(.shift("lr")) shifter_1 (.in(main_1_out_4), .\dist (3'b011), .out(shifter_1_out));
  Bit_Extender #(.out_width(5)) bit_extender_1 (.in(shifter_1_out), .out(out_7));
  Register register_1 (.D(BallX_POST), .en(reflectX), .Q(BallX_PRE), .clk(clock), .clr(reset));
  Register register_2 (.D(BallY_POST), .en(reflect), .Q(BallY_PRE), .clk(clock), .clr(reset));
  Register register_3 (.D(Vx_POST), .Q(Vx_PRE), .clk(clock), .clr(reset));  // open: en
  Register register_4 (.D(Vy_POST), .Q(Vy_PRE), .clk(clock), .clr(reset));  // open: en
  _8_to_3 u_8_to_3_1 (.in_1(Vx_POST), .out_2(VXYTOROB[2:0]));
  _8_to_3 u_8_to_3_2 (.in_1(Vy_POST), .out_2(VXYTOROB[5:3]));
  is_hit_the_right is_hit_the_right_1 (
    .in_1(BallX_POST), .in_2(BallY_POST), .leftBat(out_7), .out_4(is_hit_the_right_1_out_4));
  Adder adder_1 (.a(Vx_PRE), .b(BallX_PRE), .out(adder_1_out), .cout(X_C_flag));  // open: cin
  Adder adder_2 (.a(BallY_PRE), .b(Vy_PRE), .out(adder_2_out), .cout(Y_C_flag));  // open: cin
  assign BallY_POST = nrun_prime ? adder_2_out : 8'bz;  // Controlled_Buffer controlled_buffer_6
  not not_2 (rightref, is_hit_the_right_1_out_4);
  Multiplexer multiplexer_1 (.in0(1'b0), .in1(1'b1), .out(multiplexer_1_out), .sel(Y_C_flag));  // open: en
  Multiplexer multiplexer_2 (.in0(1'b1), .in1(1'b0), .out(multiplexer_2_out), .sel(Y_C_flag));  // open: en
  assign BallX_POST = nrun_prime ? adder_1_out : 8'bz;  // Controlled_Buffer controlled_buffer_7
  is_hit_the_left is_hit_the_left_1 (
    .in_1(BallX_POST), .in_2(BallY_POST), .leftBat(LeftBat), .out_4(is_hit_the_left_1_out_4));
  Multiplexer multiplexer_3 (
    .in0(multiplexer_1_out), .in1(multiplexer_2_out), .out(multiplexer_3_out), .sel(Vy_PRE[7]));  // open: en
  Shifter #(.shift("lr")) shifter_2 (.in(BallX_PRE), .\dist (3'b011), .out(shifter_2_out));
  Shifter #(.shift("lr")) shifter_3 (.in(BallY_PRE), .\dist (3'b011), .out(shifter_3_out));
  not not_3 (reflrctbtlft, is_hit_the_left_1_out_4);
  not not_4 (reflect, multiplexer_3_out);
  Bit_Extender #(.out_width(5)) bit_extender_2 (.in(shifter_2_out), .out(BallX_2));
  Bit_Extender #(.out_width(5)) bit_extender_3 (.in(shifter_3_out), .out(BallY_2));
  assign controlled_buffer_8_out = nrun_prime ? Vx_PRE : 8'bz;  // Controlled_Buffer controlled_buffer_8
  invert_V invert_v_1 (.in_1(Vx_PRE), .out_2(invert_v_1_out_2));
  assign controlled_buffer_9_out = nrun_prime ? Vy_PRE : 8'bz;  // Controlled_Buffer controlled_buffer_9
  assign controlled_buffer_10_out = reflectX ? controlled_buffer_8_out : 8'bz;  // Controlled_Buffer controlled_buffer_10
  not not_5 (not_5_out, reflectX);
  and and_1 (reflectX, reflrctbtlft, reflect_t, rightref);
  assign controlled_buffer_11_out = reflect ? controlled_buffer_9_out : 8'bz;  // Controlled_Buffer controlled_buffer_11
  invert_V invert_v_2 (.in_1(Vy_PRE), .out_2(invert_v_2_out_2));
  Multiplexer #(.width(8)) multiplexer_4 (
    .in0(Vx_PRE), .in1(invert_v_1_out_2), .out(controlled_buffer_10_out), .sel(not_5_out));  // open: en
  Multiplexer #(.width(8)) multiplexer_5 (
    .in0(Vy_PRE), .in1(invert_v_2_out_2), .out(controlled_buffer_11_out), .sel(not_6_out));  // open: en
  not not_6 (not_6_out, reflect);
  assign Vx_POST = nrun_prime ? controlled_buffer_10_out : 8'bz;  // Controlled_Buffer controlled_buffer_12
  assign Vy_POST = nrun_prime ? controlled_buffer_11_out : 8'bz;  // Controlled_Buffer controlled_buffer_13
  Multiplexer multiplexer_6 (.in0(1'b1), .in1(1'b0), .out(multiplexer_6_out), .sel(X_C_flag));  // open: en
  Multiplexer multiplexer_7 (.in0(1'b0), .in1(1'b1), .out(multiplexer_7_out), .sel(X_C_flag));  // open: en
  Multiplexer multiplexer_8 (
    .in0(multiplexer_7_out), .in1(multiplexer_6_out), .out(multiplexer_8_out), .sel(Vx_PRE[7]));  // open: en
  not not_7 (reflect_t, multiplexer_8_out);

  // Other names for the same wires on the sheet: RightBATEA[4:0] = out_7

  // Notes on the sheet:
  //   3bitY
  //   3bitX
  //   |
  //   \/
  //   here (between buffers )
  //   some procces that changes the Vxy....
  //   (or not)
endmodule

module videoSub (
  input  [4:0] in_1,
  input  [4:0] in_2,
  input  [4:0] in_3,
  input  [4:0] in_4,
  input  [4:0] in_5,
  output [31:0] out_6,
  output [31:0] out_7,
  output [31:0] out_8,
  output [31:0] out_9,
  output [31:0] out_10,
  output [31:0] out_11,
  output [31:0] out_12,
  output [31:0] out_13,
  output [4:0] BallX,
  output [4:0] BallY,
  output [4:0] rightBat,
  output [4:0] leftBat,
  output [4:0] chipID
);

  wire [4:0] videochip_1_ballx_2, videochip_1_bally_2, videochip_1_chipid_2, videochip_1_leftbat_2,
       videochip_1_rightbat_2, videochip_2_ballx_2, videochip_2_bally_2, videochip_2_chipid_2,
       videochip_2_leftbat_2, videochip_2_rightbat_2, videochip_3_ballx_2, videochip_3_bally_2,
       videochip_3_chipid_2, videochip_3_leftbat_2, videochip_3_rightbat_2, videochip_4_ballx_2,
       videochip_4_bally_2, videochip_4_chipid_2, videochip_4_leftbat_2, videochip_4_rightbat_2,
       videochip_5_ballx_2, videochip_5_bally_2, videochip_5_chipid_2, videochip_5_leftbat_2,
       videochip_5_rightbat_2, videochip_6_ballx_2, videochip_6_bally_2, videochip_6_chipid_2,
       videochip_6_leftbat_2, videochip_6_rightbat_2, videochip_7_ballx_2, videochip_7_bally_2,
       videochip_7_chipid_2, videochip_7_leftbat_2, videochip_7_rightbat_2;

  videochip videochip_1 (
    .chipID(in_5), .leftBat(in_4), .rightBat(in_3), .BallY(in_2), .BallX(in_1),
    .BallX_2(videochip_1_ballx_2), .BallY_2(videochip_1_bally_2), .rightBat_2(videochip_1_rightbat_2),
    .leftBat_2(videochip_1_leftbat_2), .chipID_2(videochip_1_chipid_2), .out_6(out_6));
  videochip videochip_2 (
    .chipID(videochip_1_chipid_2), .leftBat(videochip_1_leftbat_2), .rightBat(videochip_1_rightbat_2),
    .BallY(videochip_1_bally_2), .BallX(videochip_1_ballx_2), .BallX_2(videochip_2_ballx_2),
    .BallY_2(videochip_2_bally_2), .rightBat_2(videochip_2_rightbat_2), .leftBat_2(videochip_2_leftbat_2),
    .chipID_2(videochip_2_chipid_2), .out_6(out_7));
  videochip videochip_3 (
    .chipID(videochip_2_chipid_2), .leftBat(videochip_2_leftbat_2), .rightBat(videochip_2_rightbat_2),
    .BallY(videochip_2_bally_2), .BallX(videochip_2_ballx_2), .BallX_2(videochip_3_ballx_2),
    .BallY_2(videochip_3_bally_2), .rightBat_2(videochip_3_rightbat_2), .leftBat_2(videochip_3_leftbat_2),
    .chipID_2(videochip_3_chipid_2), .out_6(out_8));
  videochip videochip_4 (
    .chipID(videochip_3_chipid_2), .leftBat(videochip_3_leftbat_2), .rightBat(videochip_3_rightbat_2),
    .BallY(videochip_3_bally_2), .BallX(videochip_3_ballx_2), .BallX_2(videochip_4_ballx_2),
    .BallY_2(videochip_4_bally_2), .rightBat_2(videochip_4_rightbat_2), .leftBat_2(videochip_4_leftbat_2),
    .chipID_2(videochip_4_chipid_2), .out_6(out_9));
  videochip videochip_5 (
    .chipID(videochip_4_chipid_2), .leftBat(videochip_4_leftbat_2), .rightBat(videochip_4_rightbat_2),
    .BallY(videochip_4_bally_2), .BallX(videochip_4_ballx_2), .BallX_2(videochip_5_ballx_2),
    .BallY_2(videochip_5_bally_2), .rightBat_2(videochip_5_rightbat_2), .leftBat_2(videochip_5_leftbat_2),
    .chipID_2(videochip_5_chipid_2), .out_6(out_10));
  videochip videochip_6 (
    .chipID(videochip_5_chipid_2), .leftBat(videochip_5_leftbat_2), .rightBat(videochip_5_rightbat_2),
    .BallY(videochip_5_bally_2), .BallX(videochip_5_ballx_2), .BallX_2(videochip_6_ballx_2),
    .BallY_2(videochip_6_bally_2), .rightBat_2(videochip_6_rightbat_2), .leftBat_2(videochip_6_leftbat_2),
    .chipID_2(videochip_6_chipid_2), .out_6(out_11));
  videochip videochip_7 (
    .chipID(videochip_6_chipid_2), .leftBat(videochip_6_leftbat_2), .rightBat(videochip_6_rightbat_2),
    .BallY(videochip_6_bally_2), .BallX(videochip_6_ballx_2), .BallX_2(videochip_7_ballx_2),
    .BallY_2(videochip_7_bally_2), .rightBat_2(videochip_7_rightbat_2), .leftBat_2(videochip_7_leftbat_2),
    .chipID_2(videochip_7_chipid_2), .out_6(out_12));
  videochip videochip_8 (
    .chipID(videochip_7_chipid_2), .leftBat(videochip_7_leftbat_2), .rightBat(videochip_7_rightbat_2),
    .BallY(videochip_7_bally_2), .BallX(videochip_7_ballx_2), .BallX_2(BallX), .BallY_2(BallY),
    .rightBat_2(rightBat), .leftBat_2(leftBat), .chipID_2(chipID), .out_6(out_13));
endmodule

module _3_bit_to_8_sign (
  input  [2:0] in_1,
  output [7:0] out_2
);

  wire [2:0] adder_1_out, not_1_out;
  wire [7:0] adder_2_out, not_2_out;

  assign not_1_out = ~in_1;  // NOT_Gate not_1, 3 bits wide
  Adder #(.width(3)) adder_1 (.a(not_1_out), .b(3'b001), .out(adder_1_out));  // open: cin, cout
  Multiplexer #(.width(8)) multiplexer_1 (
    .in0({{5{1'b0}}, in_1}), .in1(adder_2_out), .out(out_2), .sel(in_1[2]));  // open: en
  assign not_2_out = ~{{5{1'b0}}, adder_1_out};  // NOT_Gate not_2, 8 bits wide
  Adder adder_2 (.a(not_2_out), .b(8'hc), .out(adder_2_out));  // open: cin, cout
endmodule

module is_hit_the_left (
  input  [7:0] in_1,
  input  [7:0] in_2,
  input  [4:0] leftBat,
  output out_4
);

  wire comparator_1_eq, comparator_2_eq, comparator_3_eq, comparator_4_eq, or_1_out;
  wire [4:0] adder_1_out, adder_2_out, bit_extender_1_out, bit_extender_2_out;
  wire [7:0] shifter_1_out, shifter_2_out;

  Shifter #(.shift("lr")) shifter_1 (.in(in_1), .\dist (3'b011), .out(shifter_1_out));
  Shifter #(.shift("lr")) shifter_2 (.in(in_2), .\dist (3'b011), .out(shifter_2_out));
  Bit_Extender #(.out_width(5)) bit_extender_1 (.in(shifter_1_out), .out(bit_extender_1_out));
  Bit_Extender #(.out_width(5)) bit_extender_2 (.in(shifter_2_out), .out(bit_extender_2_out));
  Adder #(.width(5)) adder_1 (.a(leftBat), .b(5'b00001), .out(adder_1_out));  // open: cin, cout
  Adder #(.width(5)) adder_2 (.a(leftBat), .b(5'b00010), .out(adder_2_out));  // open: cin, cout
  Comparator #(.width(5), .mode("unsigned")) comparator_1 (
    .a(bit_extender_1_out), .b(5'b00011), .eq(comparator_1_eq));  // open: gt, lt
  Comparator #(.width(5), .mode("unsigned")) comparator_2 (
    .a(bit_extender_2_out), .b(leftBat), .eq(comparator_2_eq));  // open: gt, lt
  Comparator #(.width(5), .mode("unsigned")) comparator_3 (
    .a(bit_extender_2_out), .b(adder_1_out), .eq(comparator_3_eq));  // open: gt, lt
  Comparator #(.width(5), .mode("unsigned")) comparator_4 (
    .a(bit_extender_2_out), .b(adder_2_out), .eq(comparator_4_eq));  // open: gt, lt
  and and_1 (out_4, comparator_1_eq, or_1_out);
  or or_1 (or_1_out, comparator_2_eq, comparator_3_eq, comparator_4_eq);

  // Other names for the same wires on the sheet: BallX_POST[7:0] = in_1; BallY_POST[7:0] = in_2
endmodule

module is_hit_the_right (
  input  [7:0] in_1,
  input  [7:0] in_2,
  input  [4:0] leftBat,
  output out_4
);

  wire comparator_1_eq, comparator_2_eq, comparator_3_eq, comparator_4_eq, or_1_out;
  wire [4:0] adder_1_out, adder_2_out, bit_extender_1_out, bit_extender_2_out;
  wire [7:0] shifter_1_out, shifter_2_out;

  Shifter #(.shift("lr")) shifter_1 (.in(in_1), .\dist (3'b011), .out(shifter_1_out));
  Shifter #(.shift("lr")) shifter_2 (.in(in_2), .\dist (3'b011), .out(shifter_2_out));
  Bit_Extender #(.out_width(5)) bit_extender_1 (.in(shifter_1_out), .out(bit_extender_1_out));
  Bit_Extender #(.out_width(5)) bit_extender_2 (.in(shifter_2_out), .out(bit_extender_2_out));
  Adder #(.width(5)) adder_1 (.a(leftBat), .b(5'b00001), .out(adder_1_out));  // open: cin, cout
  Adder #(.width(5)) adder_2 (.a(leftBat), .b(5'b00010), .out(adder_2_out));  // open: cin, cout
  Comparator #(.width(5), .mode("unsigned")) comparator_1 (
    .a(bit_extender_1_out), .b(5'b11100), .eq(comparator_1_eq));  // open: gt, lt
  Comparator #(.width(5), .mode("unsigned")) comparator_2 (
    .a(bit_extender_2_out), .b(leftBat), .eq(comparator_2_eq));  // open: gt, lt
  Comparator #(.width(5), .mode("unsigned")) comparator_3 (
    .a(bit_extender_2_out), .b(adder_1_out), .eq(comparator_3_eq));  // open: gt, lt
  Comparator #(.width(5), .mode("unsigned")) comparator_4 (
    .a(bit_extender_2_out), .b(adder_2_out), .eq(comparator_4_eq));  // open: gt, lt
  and and_1 (out_4, comparator_1_eq, or_1_out);
  or or_1 (or_1_out, comparator_2_eq, comparator_3_eq, comparator_4_eq);

  // Other names for the same wires on the sheet: BallX_POST[7:0] = in_1; BallY_POST[7:0] = in_2
endmodule

module invert_V (
  input  [7:0] in_1,
  output [7:0] out_2
);

  wire comparator_1_eq;
  wire [7:0] adder_1_out, not_1_out;

  assign not_1_out = ~in_1;  // NOT_Gate not_1, 8 bits wide
  Comparator comparator_1 (.a(in_1), .b(8'hfc), .eq(comparator_1_eq));  // open: gt, lt
  Adder adder_1 (.a(not_1_out), .b(8'h1), .out(adder_1_out));  // open: cin, cout
  Multiplexer #(.width(8)) multiplexer_1 (
    .in0(adder_1_out), .in1(8'h3), .out(out_2), .sel(comparator_1_eq));  // open: en
endmodule

module _8_to_3 (
  input  [7:0] in_1,
  output [2:0] out_2
);

  wire [2:0] adder_2_out, bit_extender_1_out, bit_extender_2_out, not_2_out;
  wire [7:0] adder_1_out, not_1_out;

  assign not_1_out = ~in_1;  // NOT_Gate not_1, 8 bits wide
  Bit_Extender #(.out_width(3)) bit_extender_1 (.in(in_1), .out(bit_extender_1_out));
  Adder adder_1 (.a(not_1_out), .b(8'h1), .out(adder_1_out));  // open: cin, cout
  Multiplexer #(.width(3)) multiplexer_1 (
    .in0(bit_extender_1_out), .in1(adder_2_out), .out(out_2), .sel(in_1[7]));  // open: en
  assign not_2_out = ~bit_extender_2_out;  // NOT_Gate not_2, 3 bits wide
  Bit_Extender #(.out_width(3)) bit_extender_2 (.in(adder_1_out), .out(bit_extender_2_out));
  Adder #(.width(3)) adder_2 (.a(not_2_out), .b(3'b001), .out(adder_2_out));  // open: cin, cout
endmodule
