// Logisim project tennis_fin.circ as structural Verilog
module main (
);

  wire button_out, clock_1_out, kinematic_controller_1_out_11, kinematic_controller_1_out_13, res, set_out,
       switch_1_out_2, videosub_1_is_in_menu, videosub_1_power, videosub_2_is_in_menu, videosub_2_power,
       videosub_3_is_in_menu, videosub_3_power;
  wire [2:0] kinematic_controller_1_out_12, videosub_1_level, videosub_2_level, videosub_3_level;
  wire [3:0] P_0, P_1, R_0, R_1;
  wire [4:0] joystick_1_y, joystick_2_out_2, kinematic_controller_1_ballx, kinematic_controller_1_bally,
       kinematic_controller_1_joystick, kinematic_controller_1_robot, not_1_out, videosub_1_ballx,
       videosub_1_bally, videosub_1_chipid, videosub_1_leftbat, videosub_1_rightbat, videosub_2_ballx,
       videosub_2_bally, videosub_2_chipid, videosub_2_leftbat, videosub_2_rightbat, videosub_3_ballx,
       videosub_3_bally, videosub_3_chipid, videosub_3_leftbat, videosub_3_rightbat;
  wire [31:0] videosub_1_out_9, videosub_1_out_10, videosub_1_out_11, videosub_1_out_12, videosub_1_out_13,
       videosub_1_out_14, videosub_1_out_15, videosub_1_out_16, videosub_2_out_9, videosub_2_out_10,
       videosub_2_out_11, videosub_2_out_12, videosub_2_out_13, videosub_2_out_14, videosub_2_out_15,
       videosub_2_out_16, videosub_3_out_9, videosub_3_out_10, videosub_3_out_11, videosub_3_out_12,
       videosub_3_out_13, videosub_3_out_14, videosub_3_out_15, videosub_3_out_16, videosub_4_out_9,
       videosub_4_out_10, videosub_4_out_11, videosub_4_out_12, videosub_4_out_13, videosub_4_out_14,
       videosub_4_out_15, videosub_4_out_16;

  Button button (.out(button_out));
  switch switch_1 (.tap_here_x2(button_out), .out_2(switch_1_out_2));
  Button u_RES (.out(res));
  // Probe on joystick_1_y
  Joystick_part #(.bits(5)) joystick_1 (.y(joystick_1_y));  // open: x
  Button set (.out(set_out));
  Joystick joystick_2 (.in_1(joystick_1_y), .out_2(joystick_2_out_2));
  assign not_1_out = ~joystick_2_out_2;  // NOT_Gate not_1, 5 bits wide
  Kinematic_controller kinematic_controller_1 (
    .reset(res), .BallX(kinematic_controller_1_ballx), .BallY(kinematic_controller_1_bally),
    .clock(clock_1_out), .out_14(R_1), .out_15(R_0), .LeftBat(not_1_out), .out_16(P_1), .out_17(P_0),
    .JoyStick(kinematic_controller_1_joystick), .Robot(kinematic_controller_1_robot), .power(switch_1_out_2),
    .out_11(kinematic_controller_1_out_11), .Inputs(set_out), .out_13(kinematic_controller_1_out_13),
    .out_12(kinematic_controller_1_out_12));  // open: in_6
  Clock clock_1 (.out(clock_1_out));
  // Probe on not_1_out
  Hex_Digit_Display hex_digit_display_1 (.value(P_1));  // open: dp
  Hex_Digit_Display hex_digit_display_2 (.value(P_0));  // open: dp
  videoSub videosub_1 (
    .out_9(videosub_1_out_9), .out_10(videosub_1_out_10), .out_11(videosub_1_out_11),
    .out_12(videosub_1_out_12), .out_13(videosub_1_out_13), .out_14(videosub_1_out_14),
    .out_15(videosub_1_out_15), .out_16(videosub_1_out_16), .in_1(kinematic_controller_1_ballx),
    .in_2(kinematic_controller_1_bally), .in_3(kinematic_controller_1_robot),
    .in_4(kinematic_controller_1_joystick), .in_5({5{1'b0}}), .BallX(videosub_1_ballx),
    .BallY(videosub_1_bally), .rightBat(videosub_1_rightbat), .leftBat(videosub_1_leftbat),
    .chipID(videosub_1_chipid), .in_6(kinematic_controller_1_out_11), .power(videosub_1_power),
    .in_7(kinematic_controller_1_out_13), .in_8(kinematic_controller_1_out_12), .level(videosub_1_level),
    .is_in_menu(videosub_1_is_in_menu));
  DotMatrix #(.matrixcols(32), .matrixrows(32)) dotmatrix_1 (
    .col0(videosub_1_out_9), .col1(videosub_1_out_10), .col2(videosub_1_out_11), .col3(videosub_1_out_12),
    .col4(videosub_1_out_13), .col5(videosub_1_out_14), .col6(videosub_1_out_15), .col7(videosub_1_out_16),
    .col8(videosub_2_out_9), .col9(videosub_2_out_10), .col10(videosub_2_out_11), .col11(videosub_2_out_12),
    .col12(videosub_2_out_13), .col13(videosub_2_out_14), .col14(videosub_2_out_15),
    .col15(videosub_2_out_16), .col16(videosub_3_out_9), .col17(videosub_3_out_10),
    .col18(videosub_3_out_11), .col19(videosub_3_out_12), .col20(videosub_3_out_13),
    .col21(videosub_3_out_14), .col22(videosub_3_out_15), .col23(videosub_3_out_16),
    .col24(videosub_4_out_9), .col25(videosub_4_out_10), .col26(videosub_4_out_11),
    .col27(videosub_4_out_12), .col28(videosub_4_out_13), .col29(videosub_4_out_14),
    .col30(videosub_4_out_15), .col31(videosub_4_out_16));
  videoSub videosub_2 (
    .out_9(videosub_2_out_9), .out_10(videosub_2_out_10), .out_11(videosub_2_out_11),
    .out_12(videosub_2_out_12), .out_13(videosub_2_out_13), .out_14(videosub_2_out_14),
    .out_15(videosub_2_out_15), .out_16(videosub_2_out_16), .in_1(videosub_1_ballx), .in_2(videosub_1_bally),
    .in_3(videosub_1_rightbat), .in_4(videosub_1_leftbat), .in_5(videosub_1_chipid),
    .BallX(videosub_2_ballx), .BallY(videosub_2_bally), .rightBat(videosub_2_rightbat),
    .leftBat(videosub_2_leftbat), .chipID(videosub_2_chipid), .in_6(videosub_1_power),
    .power(videosub_2_power), .in_7(videosub_1_is_in_menu), .in_8(videosub_1_level),
    .level(videosub_2_level), .is_in_menu(videosub_2_is_in_menu));
  videoSub videosub_3 (
    .out_9(videosub_3_out_9), .out_10(videosub_3_out_10), .out_11(videosub_3_out_11),
    .out_12(videosub_3_out_12), .out_13(videosub_3_out_13), .out_14(videosub_3_out_14),
    .out_15(videosub_3_out_15), .out_16(videosub_3_out_16), .in_1(videosub_2_ballx), .in_2(videosub_2_bally),
    .in_3(videosub_2_rightbat), .in_4(videosub_2_leftbat), .in_5(videosub_2_chipid),
    .BallX(videosub_3_ballx), .BallY(videosub_3_bally), .rightBat(videosub_3_rightbat),
    .leftBat(videosub_3_leftbat), .chipID(videosub_3_chipid), .in_6(videosub_2_power),
    .power(videosub_3_power), .in_7(videosub_2_is_in_menu), .in_8(videosub_2_level),
    .level(videosub_3_level), .is_in_menu(videosub_3_is_in_menu));
  videoSub videosub_4 (
    .out_9(videosub_4_out_9), .out_10(videosub_4_out_10), .out_11(videosub_4_out_11),
    .out_12(videosub_4_out_12), .out_13(videosub_4_out_13), .out_14(videosub_4_out_14),
    .out_15(videosub_4_out_15), .out_16(videosub_4_out_16), .in_1(videosub_3_ballx), .in_2(videosub_3_bally),
    .in_3(videosub_3_rightbat), .in_4(videosub_3_leftbat), .in_5(videosub_3_chipid), .in_6(videosub_3_power),
    .in_7(videosub_3_is_in_menu), .in_8(videosub_3_level));  // open: BallX, BallY, rightBat, leftBat, chipID, power, level, is_in_menu
  Hex_Digit_Display hex_digit_display_3 (.value(R_1));  // open: dp
  Hex_Digit_Display hex_digit_display_4 (.value(R_0));  // open: dp
endmodule

module Videochip (
  input  [4:0] BallX,
  input  [4:0] BallY,
  input  [4:0] rightBat,
  input  [4:0] leftBat,
  input  [4:0] chipID,
  input  Power,
  input  menu,
  input  [2:0] lev_prime,
  output [31:0] out_9,
  output [4:0] BallX_2,
  output [4:0] BallY_2,
  output [4:0] rightBat_2,
  output [4:0] leftBat_2,
  output [4:0] chipID_2,
  output Power_2,
  output out_16,
  output [2:0] out_17
);

  wire comparator_1_eq, comparator_2_eq, comparator_3_eq;
  wire [31:0] decoder_1_out0, decoder_2_out0, decoder_3_out0, menu_data, multiplexer_2_out,
       multiplexer_3_out, multiplexer_4_out, multiplexer_5_out, or_1_out, or_2_out, or_3_out, shifter_1_out,
       shifter_2_out, shifter_3_out, shifter_4_out;

  Menu_graphics menu_graphics_1 (.chip_id(chipID), .level(lev_prime), .out_3(menu_data));
  Adder #(.width(5)) adder_1 (.a(chipID), .b(5'b00001), .out(chipID_2));  // open: cin, cout
  Comparator #(.width(5), .mode("unsigned")) comparator_1 (
    .a(BallX), .b(chipID), .eq(comparator_1_eq));  // open: gt, lt
  Comparator #(.width(5), .mode("unsigned")) comparator_2 (
    .a(chipID), .b(5'b00011), .eq(comparator_2_eq));  // open: gt, lt
  Comparator #(.width(5), .mode("unsigned")) comparator_3 (
    .a(chipID), .b(5'b11100), .eq(comparator_3_eq));  // open: gt, lt
  // Probe on 5'b11100
  Decoder #(.select(5), .enable("false")) decoder_1 (
    .out0(decoder_1_out0[0]), .out1(decoder_1_out0[1]), .out2(decoder_1_out0[2]), .out3(decoder_1_out0[3]),
    .out4(decoder_1_out0[4]), .out5(decoder_1_out0[5]), .out6(decoder_1_out0[6]), .out7(decoder_1_out0[7]),
    .out8(decoder_1_out0[8]), .out9(decoder_1_out0[9]), .out10(decoder_1_out0[10]),
    .out11(decoder_1_out0[11]), .out12(decoder_1_out0[12]), .out13(decoder_1_out0[13]),
    .out14(decoder_1_out0[14]), .out15(decoder_1_out0[15]), .out16(decoder_1_out0[16]),
    .out17(decoder_1_out0[17]), .out18(decoder_1_out0[18]), .out19(decoder_1_out0[19]),
    .out20(decoder_1_out0[20]), .out21(decoder_1_out0[21]), .out22(decoder_1_out0[22]),
    .out23(decoder_1_out0[23]), .out24(decoder_1_out0[24]), .out25(decoder_1_out0[25]),
    .out26(decoder_1_out0[26]), .out27(decoder_1_out0[27]), .out28(decoder_1_out0[28]),
    .out29(decoder_1_out0[29]), .out30(decoder_1_out0[30]), .out31(decoder_1_out0[31]), .sel(rightBat));
  Decoder #(.select(5), .enable("false")) decoder_2 (
    .out0(decoder_2_out0[0]), .out1(decoder_2_out0[1]), .out2(decoder_2_out0[2]), .out3(decoder_2_out0[3]),
    .out4(decoder_2_out0[4]), .out5(decoder_2_out0[5]), .out6(decoder_2_out0[6]), .out7(decoder_2_out0[7]),
    .out8(decoder_2_out0[8]), .out9(decoder_2_out0[9]), .out10(decoder_2_out0[10]),
    .out11(decoder_2_out0[11]), .out12(decoder_2_out0[12]), .out13(decoder_2_out0[13]),
    .out14(decoder_2_out0[14]), .out15(decoder_2_out0[15]), .out16(decoder_2_out0[16]),
    .out17(decoder_2_out0[17]), .out18(decoder_2_out0[18]), .out19(decoder_2_out0[19]),
    .out20(decoder_2_out0[20]), .out21(decoder_2_out0[21]), .out22(decoder_2_out0[22]),
    .out23(decoder_2_out0[23]), .out24(decoder_2_out0[24]), .out25(decoder_2_out0[25]),
    .out26(decoder_2_out0[26]), .out27(decoder_2_out0[27]), .out28(decoder_2_out0[28]),
    .out29(decoder_2_out0[29]), .out30(decoder_2_out0[30]), .out31(decoder_2_out0[31]), .sel(BallY));
  Decoder #(.select(5), .enable("false")) decoder_3 (
    .out0(decoder_3_out0[0]), .out1(decoder_3_out0[1]), .out2(decoder_3_out0[2]), .out3(decoder_3_out0[3]),
    .out4(decoder_3_out0[4]), .out5(decoder_3_out0[5]), .out6(decoder_3_out0[6]), .out7(decoder_3_out0[7]),
    .out8(decoder_3_out0[8]), .out9(decoder_3_out0[9]), .out10(decoder_3_out0[10]),
    .out11(decoder_3_out0[11]), .out12(decoder_3_out0[12]), .out13(decoder_3_out0[13]),
    .out14(decoder_3_out0[14]), .out15(decoder_3_out0[15]), .out16(decoder_3_out0[16]),
    .out17(decoder_3_out0[17]), .out18(decoder_3_out0[18]), .out19(decoder_3_out0[19]),
    .out20(decoder_3_out0[20]), .out21(decoder_3_out0[21]), .out22(decoder_3_out0[22]),
    .out23(decoder_3_out0[23]), .out24(decoder_3_out0[24]), .out25(decoder_3_out0[25]),
    .out26(decoder_3_out0[26]), .out27(decoder_3_out0[27]), .out28(decoder_3_out0[28]),
    .out29(decoder_3_out0[29]), .out30(decoder_3_out0[30]), .out31(decoder_3_out0[31]), .sel(leftBat));
  Multiplexer #(.width(32), .enable("false")) multiplexer_1 (
    .in0({32{1'b1}}), .in1(multiplexer_2_out), .out(out_9), .sel(Power));
  Multiplexer #(.width(32), .enable("false")) multiplexer_2 (
    .in0(or_3_out), .in1(menu_data), .out(multiplexer_2_out), .sel(menu));
  Multiplexer #(.width(32), .enable("false")) multiplexer_3 (
    .in0({32{1'b0}}), .in1(decoder_2_out0), .out(multiplexer_3_out), .sel(comparator_1_eq));
  Multiplexer #(.width(32), .enable("false")) multiplexer_4 (
    .in0({32{1'b0}}), .in1(decoder_3_out0), .out(multiplexer_4_out), .sel(comparator_2_eq));
  Multiplexer #(.width(32), .enable("false")) multiplexer_5 (
    .in0({32{1'b0}}), .in1(decoder_1_out0), .out(multiplexer_5_out), .sel(comparator_3_eq));
  Shifter #(.width(32)) shifter_1 (.in(multiplexer_4_out), .\dist (5'b00001), .out(shifter_1_out));
  Shifter #(.width(32)) shifter_2 (.in(multiplexer_5_out), .\dist (5'b00001), .out(shifter_2_out));
  Shifter #(.width(32)) shifter_3 (.in(shifter_1_out), .\dist (5'b00001), .out(shifter_3_out));
  Shifter #(.width(32)) shifter_4 (.in(shifter_2_out), .\dist (5'b00001), .out(shifter_4_out));
  assign or_1_out = multiplexer_4_out | shifter_1_out | shifter_3_out;  // OR_Gate or_1, 32 bits wide
  assign or_2_out = multiplexer_5_out | shifter_2_out | shifter_4_out;  // OR_Gate or_2, 32 bits wide
  assign or_3_out = multiplexer_3_out | or_1_out | or_2_out;  // OR_Gate or_3, 32 bits wide

  assign BallX_2 = BallX;
  assign BallY_2 = BallY;
  assign leftBat_2 = leftBat;
  assign out_16 = menu;
  assign out_17 = lev_prime;
  assign Power_2 = Power;
  assign rightBat_2 = rightBat;

  // Other names for the same wires on the sheet: level[2:0] = lev_prime

  // Notes on the sheet:
  //   Menu graphics
  //   no power -> only 1's (black pixels in our case)
endmodule

module Kinematic_controller (
  input  Inputs,
  input  [4:0] LeftBat,
  input  reset,
  input  clock,
  input  power,
  input  in_6,
  output [4:0] Robot,
  output [4:0] JoyStick,
  output [4:0] BallX,
  output [4:0] BallY,
  output out_11,
  output [2:0] out_12,
  output out_13,
  output [3:0] out_14,
  output [3:0] out_15,
  output [3:0] out_16,
  output [3:0] out_17
);

  wire and_1_out, and_2_out, and_5_out, and_6_out, and_8_out, and_9_out, and_10_out, and_11_out, C_left_flag,
       C_right_flag, clock_t, comparator_1_gt, comparator_3_eq, comparator_3_gt, comparator_3_lt,
       comparator_4_lt, comparator_7_gt, comparator_8_eq, comparator_9_eq, comparator_10_eq,
       comparator_11_eq, counter_1_q, is_hit_bat_1_hits_star, is_hit_bat_2_hits_star, left_reflect,
       level_1_no_start, multiplexer_1_out, multiplexer_2_out, multiplexer_5_out, multiplexer_6_out,
       NO_NAGIB, not_2_out, not_4_out, not_5_out, not_6_out, not_7_out, not_8_out, not_9_out, not_10_out,
       not_11_out, not_12_out, not_13_out, not_14_out, not_15_out, not_16_out, not_17_out, not_18_out,
       not_19_out, not_20_out, not_21_out, not_22_out, nrun_prime, or_2_out, or_3_out, P_0_reset, R_0_reset,
       reflect, reflect_t, reflectX, reset_t, right_reflect, stop_P, stop_R, X_C_flag, Y_C_flag;
  wire [2:0] controlled_buffer_1_out, controlled_buffer_2_out, set_Vx, set_Vy;
  wire [4:0] controlled_buffer_5_out, controlled_buffer_6_out, controlled_buffer_10_out, RightBAT_smooth;
  wire [5:0] VXY_8bit;
  wire [7:0] adder_1_out, adder_2_out, adder_3_out, adder_6_out, adder_8_out, BallX_POST_sum, BallX_PRE_SUM,
       BallY_POST_sum, BallY_PRE_SUM, controlled_buffer_3_out, controlled_buffer_4_out,
       controlled_buffer_13_out, controlled_buffer_14_out, counter_9_q, difficulty_mechanics_1_right_bat_fin,
       input_output_1_out_7, invert_v_1_out_2, invert_v_2_out_2, player_score_update, RightBAT_tmp,
       robot_score_update, shifter_1_out, shifter_2_out, shifter_3_out, Vx_POST, Vx_PRE, Vy_POST, Vy_PRE;
  wire [7:4] counter_3_q, counter_4_q;

  not not_1 (out_13, level_1_no_start);
  Level level_1 (
    .res(reset_t), .set(Inputs), .in_3(LeftBat), .no_start(level_1_no_start), .hard(out_12[0]),
    .norm(out_12[1]), .ez(out_12[2]));
  _3_bit_to_8_sign u_3_bit_to_8_sign_1 (.in_1(controlled_buffer_1_out), .out_2(Vx_POST));
  assign controlled_buffer_1_out = out_13 ? set_Vx : 3'bz;  // Controlled_Buffer controlled_buffer_1
  _3_bit_to_8_sign u_3_bit_to_8_sign_2 (.in_1(controlled_buffer_2_out), .out_2(Vy_POST));
  assign controlled_buffer_2_out = out_13 ? set_Vy : 3'bz;  // Controlled_Buffer controlled_buffer_2
  or or_1 (reset_t, reset, not_2_out);
  not not_2 (not_2_out, power);
  Counter #(.width(1), .max('h1)) counter_1 (.Q(counter_1_q), .clk(clock));  // open: load, D, count, carry, clr
  Input_Output input_output_1 (
    .in_1({2'b00, VXY_8bit}), .out_7(input_output_1_out_7), .block(NO_NAGIB), .INPUT_BallX_8b(BallX_PRE_SUM),
    .INPUT_BallY_8b(BallY_PRE_SUM), .res(reset_t), .run(out_13));
  not not_3 (nrun_prime, out_13);
  Counter #(.width(1), .max('h1)) counter_2 (.Q(clock_t), .clk(counter_1_q));  // open: load, D, count, carry, clr
  Multiplexer multiplexer_1 (.in0(1'b0), .in1(1'b1), .out(multiplexer_1_out), .sel(Y_C_flag));  // open: en
  Multiplexer multiplexer_2 (.in0(1'b1), .in1(1'b0), .out(multiplexer_2_out), .sel(Y_C_flag));  // open: en
  Register register_1 (.D(Vx_POST), .Q(Vx_PRE), .clk(clock_t), .clr(reset_t));  // open: en
  Register register_2 (.D(Vy_POST), .Q(Vy_PRE), .clk(clock_t), .clr(reset_t));  // open: en
  Multiplexer multiplexer_3 (
    .in0(multiplexer_1_out), .in1(multiplexer_2_out), .out(reflect), .sel(Vy_PRE[7]));  // open: en
  Difficulty_mechanics difficulty_mechanics_1 (
    .level(out_12), .right_bat(RightBAT_tmp), .VY(set_Vy), .VX_2(set_Vx),
    .right_bat_fin(difficulty_mechanics_1_right_bat_fin), .ball_X(BallX_PRE_SUM), .VX({2'b00, VXY_8bit}));
  assign controlled_buffer_3_out = nrun_prime ? Vy_PRE : 8'bz;  // Controlled_Buffer controlled_buffer_3
  invert_V invert_v_1 (.in_1(Vy_PRE), .out_2(invert_v_1_out_2));
  Adder adder_1 (.a(input_output_1_out_7), .b(8'hf6), .out(adder_1_out));  // open: cin, cout
  Multiplexer #(.width(8), .enable("false")) multiplexer_4 (
    .in0(adder_1_out), .in1(input_output_1_out_7), .out(RightBAT_tmp), .sel(not_4_out));
  not not_4 (not_4_out, comparator_1_gt);
  Comparator #(.mode("unsigned")) comparator_1 (
    .a(input_output_1_out_7), .b(8'h10), .gt(comparator_1_gt));  // open: eq, lt
  Adder adder_2 (.a(Vx_PRE), .b(BallX_PRE_SUM), .out(adder_2_out), .cout(X_C_flag));  // open: cin
  Adder adder_3 (.a(BallY_PRE_SUM), .b(Vy_PRE), .out(adder_3_out), .cout(Y_C_flag));  // open: cin
  assign controlled_buffer_4_out = not_5_out ? controlled_buffer_3_out : 8'bz;  // Controlled_Buffer controlled_buffer_4
  not not_5 (not_5_out, reflect);
  and and_1 (and_1_out, reflect, not_6_out);
  not not_6 (not_6_out, clock_t);
  Multiplexer multiplexer_5 (.in0(1'b0), .in1(1'b1), .out(multiplexer_5_out), .sel(X_C_flag));  // open: en
  Multiplexer multiplexer_6 (.in0(1'b1), .in1(1'b0), .out(multiplexer_6_out), .sel(X_C_flag));  // open: en
  Comparator #(.mode("unsigned")) comparator_2 (.a(BallX_PRE_SUM), .b(8'h9f), .gt(NO_NAGIB));  // open: eq, lt
  assign controlled_buffer_5_out = comparator_3_gt ? Robot : 5'bz;  // Controlled_Buffer controlled_buffer_5
  Comparator #(.width(5), .mode("unsigned")) comparator_3 (
    .a(RightBAT_smooth), .b(Robot), .gt(comparator_3_gt), .eq(comparator_3_eq), .lt(comparator_3_lt));
  assign controlled_buffer_6_out = comparator_3_lt ? Robot : 5'bz;  // Controlled_Buffer controlled_buffer_6
  Shifter #(.shift("lr")) shifter_1 (.in(difficulty_mechanics_1_right_bat_fin), .\dist (3'b011), .out(shifter_1_out));
  assign BallX_POST_sum = nrun_prime ? adder_2_out : 8'bz;  // Controlled_Buffer controlled_buffer_7
  assign BallY_POST_sum = nrun_prime ? adder_3_out : 8'bz;  // Controlled_Buffer controlled_buffer_8
  assign Vy_POST = nrun_prime ? controlled_buffer_4_out : 8'bz;  // Controlled_Buffer controlled_buffer_9
  Multiplexer #(.width(8), .enable("false")) multiplexer_7 (
    .in0(Vy_PRE), .in1(invert_v_1_out_2), .out(controlled_buffer_4_out), .sel(and_1_out));
  Multiplexer multiplexer_8 (
    .in0(multiplexer_5_out), .in1(multiplexer_6_out), .out(reflect_t), .sel(Vx_PRE[7]));  // open: en
  assign controlled_buffer_10_out = comparator_3_eq ? Robot : 5'bz;  // Controlled_Buffer controlled_buffer_10
  Adder #(.width(5)) adder_4 (
    .a(controlled_buffer_5_out), .b(5'b00001), .out(controlled_buffer_10_out));  // open: cin, cout
  Adder #(.width(5)) adder_5 (
    .a(controlled_buffer_6_out), .b({5{1'b1}}), .out(controlled_buffer_10_out));  // open: cin, cout
  Bit_Extender #(.out_width(5)) bit_extender_1 (.in(shifter_1_out), .out(RightBAT_smooth));
  _8_to_3 u_8_to_3_1 (.in_1(Vx_POST), .out_2(VXY_8bit[2:0]));
  _8_to_3 u_8_to_3_2 (.in_1(Vy_POST), .out_2(VXY_8bit[5:3]));
  not not_7 (not_7_out, NO_NAGIB);
  Register #(.width(5)) register_3 (
    .D(controlled_buffer_10_out), .en(not_7_out), .Q(Robot), .clk(clock_t));  // open: clr
  assign BallX_POST_sum = out_13 ? 8'h7f : 8'bz;  // Controlled_Buffer controlled_buffer_11
  assign BallY_POST_sum = out_13 ? 8'h7f : 8'bz;  // Controlled_Buffer controlled_buffer_12
  assign controlled_buffer_13_out = nrun_prime ? Vx_PRE : 8'bz;  // Controlled_Buffer controlled_buffer_13
  assign controlled_buffer_14_out = not_8_out ? controlled_buffer_13_out : 8'bz;  // Controlled_Buffer controlled_buffer_14
  not not_8 (not_8_out, reflectX);
  invert_V invert_v_2 (.in_1(Vx_PRE), .out_2(invert_v_2_out_2));
  not not_9 (not_9_out, left_reflect);
  and and_2 (and_2_out, not_9_out, not_10_out, not_11_out);
  not not_10 (not_10_out, reflect_t);
  not not_11 (not_11_out, right_reflect);
  Register register_4 (.D(BallX_POST_sum), .en(not_12_out), .Q(BallX_PRE_SUM), .clk(clock_t), .clr(reset_t));
  not not_12 (not_12_out, reflect_t);
  Register register_5 (.D(BallY_POST_sum), .en(not_13_out), .Q(BallY_PRE_SUM), .clk(clock_t), .clr(reset_t));
  not not_13 (not_13_out, reflect);
  assign Vx_POST = nrun_prime ? controlled_buffer_14_out : 8'bz;  // Controlled_Buffer controlled_buffer_15
  Multiplexer #(.width(8), .enable("false")) multiplexer_9 (
    .in0(Vx_PRE), .in1(invert_v_2_out_2), .out(controlled_buffer_14_out), .sel(reflectX));
  not not_14 (not_14_out, and_2_out);
  not not_15 (not_15_out, clock_t);
  and and_3 (reflectX, not_14_out, not_15_out);
  Adder adder_6 (.a(BallX_PRE_SUM), .b(8'he4), .out(adder_6_out));  // open: cin, cout
  not not_16 (not_16_out, C_left_flag);
  is_hit_bat is_hit_bat_1 (.BallY(BallY_PRE_SUM), .hits_star(is_hit_bat_1_hits_star), .Bat(LeftBat));
  Adder adder_7 (.a(Vx_PRE), .b(adder_6_out), .cout(C_left_flag));  // open: out, cin
  and and_4 (left_reflect, not_16_out, is_hit_bat_1_hits_star, Vx_PRE[7]);
  Shifter #(.shift("lr")) shifter_2 (.in(BallX_PRE_SUM), .\dist (3'b011), .out(shifter_2_out));
  Shifter #(.shift("lr")) shifter_3 (.in(BallY_PRE_SUM), .\dist (3'b011), .out(shifter_3_out));
  Comparator #(.mode("unsigned")) comparator_4 (.a(BallX_POST_sum), .b(8'h15), .lt(comparator_4_lt));  // open: gt, eq
  Bit_Extender #(.out_width(5)) bit_extender_2 (.in(shifter_2_out), .out(BallX));
  Bit_Extender #(.out_width(5)) bit_extender_3 (.in(shifter_3_out), .out(BallY));
  Comparator #(.width(4), .mode("unsigned")) comparator_5 (
    .a(robot_score_update[3:0]), .b(4'b1010), .eq(R_0_reset));  // open: gt, lt
  and and_5 (and_5_out, R_0_reset, not_21_out);
  Comparator #(.width(4), .mode("unsigned")) comparator_6 (
    .a(player_score_update[3:0]), .b(4'b1010), .eq(P_0_reset));  // open: gt, lt
  and and_6 (and_6_out, P_0_reset, not_18_out);
  Comparator #(.mode("unsigned")) comparator_7 (.a(BallX_POST_sum), .b(8'he9), .gt(comparator_7_gt));  // open: eq, lt
  Adder adder_8 (.a(BallX_PRE_SUM), .b(8'h1b), .out(adder_8_out));  // open: cin, cout
  and and_7 (right_reflect, C_right_flag, is_hit_bat_2_hits_star, not_17_out);
  not not_17 (not_17_out, Vx_PRE[7]);
  is_hit_bat is_hit_bat_2 (.BallY(BallY_PRE_SUM), .hits_star(is_hit_bat_2_hits_star), .Bat(Robot));
  Comparator #(.width(4), .mode("unsigned")) comparator_8 (
    .a(robot_score_update[3:0]), .b(4'b1001), .eq(comparator_8_eq));  // open: gt, lt
  Counter #(.max('h9)) counter_3 (
    .Q({counter_3_q, out_14}), .clk(and_5_out), .clr(reset_t));  // open: load, D, count, carry
  Comparator #(.width(4), .mode("unsigned")) comparator_9 (
    .a(player_score_update[3:0]), .b(4'b1001), .eq(comparator_9_eq));  // open: gt, lt
  Counter #(.max('h9)) counter_4 (
    .Q({counter_4_q, out_16}), .clk(and_6_out), .clr(reset_t));  // open: load, D, count, carry
  not not_18 (not_18_out, comparator_11_eq);
  and and_8 (and_8_out, reflect_t, comparator_4_lt, not_19_out);
  not not_19 (not_19_out, X_C_flag);
  and and_9 (and_9_out, X_C_flag, comparator_7_gt, reflect_t);
  Adder adder_9 (.a(Vx_PRE), .b(adder_8_out), .cout(C_right_flag));  // open: out, cin
  Register #(.width(4)) register_6 (
    .D(robot_score_update[3:0]), .en(not_20_out), .Q(out_15), .clk(clock_t), .clr(reset_t));
  not not_20 (not_20_out, stop_R);
  and and_10 (and_10_out, comparator_8_eq, comparator_10_eq);
  not not_21 (not_21_out, comparator_10_eq);
  Comparator #(.mode("unsigned")) comparator_10 (
    .a({counter_3_q, out_14}), .b(8'h9), .eq(comparator_10_eq));  // open: gt, lt
  Register #(.width(4)) register_7 (
    .D(player_score_update[3:0]), .en(not_22_out), .Q(out_17), .clk(clock_t), .clr(reset_t));
  not not_22 (not_22_out, stop_P);
  and and_11 (and_11_out, comparator_9_eq, comparator_11_eq);
  Comparator #(.mode("unsigned")) comparator_11 (
    .a({counter_4_q, out_16}), .b(8'h9), .eq(comparator_11_eq));  // open: gt, lt
  Counter #(.max('ha), .ongoal("load")) counter_5 (
    .D({8{1'b0}}), .Q(robot_score_update), .clk(and_8_out), .clr(or_2_out));  // open: load, count, carry
  or or_2 (or_2_out, reset_t, R_0_reset);
  Counter #(.max('ha), .ongoal("load")) counter_6 (
    .D({8{1'b0}}), .Q(player_score_update), .clk(and_9_out), .clr(or_3_out));  // open: load, count, carry
  or or_3 (or_3_out, reset_t, P_0_reset);
  Counter #(.width(1), .max('h1), .ongoal("stay")) counter_7 (
    .Q(stop_R), .clk(and_10_out), .clr(reset_t));  // open: load, D, count, carry
  Counter #(.width(1), .max('h1), .ongoal("stay")) counter_8 (
    .Q(stop_P), .clk(and_11_out), .clr(reset_t));  // open: load, D, count, carry
  Counter #(.max('ha), .ongoal("load")) counter_9 (.Q(counter_9_q), .clk(in_6));  // open: load, D, count, carry, clr

  assign JoyStick = LeftBat;
  assign out_11 = power;

  // Other names for the same wires on the sheet: level[2:0] = out_12; RightBATEA[4:0] = Robot; run = out_13;
  //   set_level = Inputs

  // Notes on the sheet:
  //   3bitX
  //   3bitY
  //   |
  //   |
  //   players selects diff level
  //   Levels of diff + menu of sel flag
  //   because of calculation depends on bottom of bat
  //   game itself
  //   |
  //   |
  //   ___________________________
  //   moves rght bat a little bit down -->
  //   ______________________________________________________
  //   _______________
  //   WALLS
  //   _________________________
  //   Vy analyze
  //   block bat
  //   animates rght bat's movements
  //   ___________________________
  //   BallX
  //   BallY
  //   ___________________________
  //   ______________________________________________________
  //   |
  //   |
  //   output
  //   Vx analyze
  //   ___________________________
  //   _______________
  //   |
  //   |
  //   |
  //   |
  //   |
  //   |
  //   |
  //   |
  //   |
  //   |
  //   |
  //   |
  //   |
  //   BATS
  //   for left
  //   _________________________
  //   __________________
  //   __________________
  //   ___________________________
  //   Outputs
  //   Score 
  //   ___________________________
  //   for right
  //   __________________
  //   ___________________________
  //   robot won
  //   player won
  //   ___________________________
  //   |
  //   |
  //   |
  //   |
  //   |
  //   |
endmodule

module videoSub (
  input  [4:0] in_1,
  input  [4:0] in_2,
  input  [4:0] in_3,
  input  [4:0] in_4,
  input  [4:0] in_5,
  input  in_6,
  input  in_7,
  input  [2:0] in_8,
  output [31:0] out_9,
  output [31:0] out_10,
  output [31:0] out_11,
  output [31:0] out_12,
  output [31:0] out_13,
  output [31:0] out_14,
  output [31:0] out_15,
  output [31:0] out_16,
  output [4:0] BallX,
  output [4:0] BallY,
  output [4:0] rightBat,
  output [4:0] leftBat,
  output [4:0] chipID,
  output power,
  output [2:0] level,
  output is_in_menu
);

  wire videochip_1_out_16, videochip_1_power_2, videochip_2_out_16, videochip_2_power_2, videochip_3_out_16,
       videochip_3_power_2, videochip_4_out_16, videochip_4_power_2, videochip_5_out_16, videochip_5_power_2,
       videochip_6_out_16, videochip_6_power_2, videochip_7_out_16, videochip_7_power_2;
  wire [2:0] videochip_1_out_17, videochip_2_out_17, videochip_3_out_17, videochip_4_out_17,
       videochip_5_out_17, videochip_6_out_17, videochip_7_out_17;
  wire [4:0] videochip_1_ballx_2, videochip_1_bally_2, videochip_1_chipid_2, videochip_1_leftbat_2,
       videochip_1_rightbat_2, videochip_2_ballx_2, videochip_2_bally_2, videochip_2_chipid_2,
       videochip_2_leftbat_2, videochip_2_rightbat_2, videochip_3_ballx_2, videochip_3_bally_2,
       videochip_3_chipid_2, videochip_3_leftbat_2, videochip_3_rightbat_2, videochip_4_ballx_2,
       videochip_4_bally_2, videochip_4_chipid_2, videochip_4_leftbat_2, videochip_4_rightbat_2,
       videochip_5_ballx_2, videochip_5_bally_2, videochip_5_chipid_2, videochip_5_leftbat_2,
       videochip_5_rightbat_2, videochip_6_ballx_2, videochip_6_bally_2, videochip_6_chipid_2,
       videochip_6_leftbat_2, videochip_6_rightbat_2, videochip_7_ballx_2, videochip_7_bally_2,
       videochip_7_chipid_2, videochip_7_leftbat_2, videochip_7_rightbat_2;

  Videochip videochip_1 (
    .chipID(in_5), .leftBat(in_4), .rightBat(in_3), .BallY(in_2), .BallX(in_1),
    .BallX_2(videochip_1_ballx_2), .BallY_2(videochip_1_bally_2), .rightBat_2(videochip_1_rightbat_2),
    .leftBat_2(videochip_1_leftbat_2), .chipID_2(videochip_1_chipid_2), .out_9(out_9), .Power(in_6),
    .Power_2(videochip_1_power_2), .menu(in_7), .lev_prime(in_8), .out_16(videochip_1_out_16),
    .out_17(videochip_1_out_17));
  Videochip videochip_2 (
    .chipID(videochip_1_chipid_2), .leftBat(videochip_1_leftbat_2), .rightBat(videochip_1_rightbat_2),
    .BallY(videochip_1_bally_2), .BallX(videochip_1_ballx_2), .BallX_2(videochip_2_ballx_2),
    .BallY_2(videochip_2_bally_2), .rightBat_2(videochip_2_rightbat_2), .leftBat_2(videochip_2_leftbat_2),
    .chipID_2(videochip_2_chipid_2), .out_9(out_10), .Power(videochip_1_power_2),
    .Power_2(videochip_2_power_2), .menu(videochip_1_out_16), .lev_prime(videochip_1_out_17),
    .out_16(videochip_2_out_16), .out_17(videochip_2_out_17));
  Videochip videochip_3 (
    .chipID(videochip_2_chipid_2), .leftBat(videochip_2_leftbat_2), .rightBat(videochip_2_rightbat_2),
    .BallY(videochip_2_bally_2), .BallX(videochip_2_ballx_2), .BallX_2(videochip_3_ballx_2),
    .BallY_2(videochip_3_bally_2), .rightBat_2(videochip_3_rightbat_2), .leftBat_2(videochip_3_leftbat_2),
    .chipID_2(videochip_3_chipid_2), .out_9(out_11), .Power(videochip_2_power_2),
    .Power_2(videochip_3_power_2), .menu(videochip_2_out_16), .lev_prime(videochip_2_out_17),
    .out_16(videochip_3_out_16), .out_17(videochip_3_out_17));
  Videochip videochip_4 (
    .chipID(videochip_3_chipid_2), .leftBat(videochip_3_leftbat_2), .rightBat(videochip_3_rightbat_2),
    .BallY(videochip_3_bally_2), .BallX(videochip_3_ballx_2), .BallX_2(videochip_4_ballx_2),
    .BallY_2(videochip_4_bally_2), .rightBat_2(videochip_4_rightbat_2), .leftBat_2(videochip_4_leftbat_2),
    .chipID_2(videochip_4_chipid_2), .out_9(out_12), .Power(videochip_3_power_2),
    .Power_2(videochip_4_power_2), .menu(videochip_3_out_16), .lev_prime(videochip_3_out_17),
    .out_16(videochip_4_out_16), .out_17(videochip_4_out_17));
  Videochip videochip_5 (
    .chipID(videochip_4_chipid_2), .leftBat(videochip_4_leftbat_2), .rightBat(videochip_4_rightbat_2),
    .BallY(videochip_4_bally_2), .BallX(videochip_4_ballx_2), .BallX_2(videochip_5_ballx_2),
    .BallY_2(videochip_5_bally_2), .rightBat_2(videochip_5_rightbat_2), .leftBat_2(videochip_5_leftbat_2),
    .chipID_2(videochip_5_chipid_2), .out_9(out_13), .Power(videochip_4_power_2),
    .Power_2(videochip_5_power_2), .menu(videochip_4_out_16), .lev_prime(videochip_4_out_17),
    .out_16(videochip_5_out_16), .out_17(videochip_5_out_17));
  Videochip videochip_6 (
    .chipID(videochip_5_chipid_2), .leftBat(videochip_5_leftbat_2), .rightBat(videochip_5_rightbat_2),
    .BallY(videochip_5_bally_2), .BallX(videochip_5_ballx_2), .BallX_2(videochip_6_ballx_2),
    .BallY_2(videochip_6_bally_2), .rightBat_2(videochip_6_rightbat_2), .leftBat_2(videochip_6_leftbat_2),
    .chipID_2(videochip_6_chipid_2), .out_9(out_14), .Power(videochip_5_power_2),
    .Power_2(videochip_6_power_2), .menu(videochip_5_out_16), .lev_prime(videochip_5_out_17),
    .out_16(videochip_6_out_16), .out_17(videochip_6_out_17));
  Videochip videochip_7 (
    .chipID(videochip_6_chipid_2), .leftBat(videochip_6_leftbat_2), .rightBat(videochip_6_rightbat_2),
    .BallY(videochip_6_bally_2), .BallX(videochip_6_ballx_2), .BallX_2(videochip_7_ballx_2),
    .BallY_2(videochip_7_bally_2), .rightBat_2(videochip_7_rightbat_2), .leftBat_2(videochip_7_leftbat_2),
    .chipID_2(videochip_7_chipid_2), .out_9(out_15), .Power(videochip_6_power_2),
    .Power_2(videochip_7_power_2), .menu(videochip_6_out_16), .lev_prime(videochip_6_out_17),
    .out_16(videochip_7_out_16), .out_17(videochip_7_out_17));
  Videochip videochip_8 (
    .chipID(videochip_7_chipid_2), .leftBat(videochip_7_leftbat_2), .rightBat(videochip_7_rightbat_2),
    .BallY(videochip_7_bally_2), .BallX(videochip_7_ballx_2), .BallX_2(BallX), .BallY_2(BallY),
    .rightBat_2(rightBat), .leftBat_2(leftBat), .chipID_2(chipID), .out_9(out_16),
    .Power(videochip_7_power_2), .Power_2(power), .menu(videochip_7_out_16), .lev_prime(videochip_7_out_17),
    .out_16(is_in_menu), .out_17(level));
endmodule

module _3_bit_to_8_sign (
  input  [2:0] in_1,
  output [7:0] out_2
);

  wire [2:0] adder_1_out, not_1_out;
  wire [7:0] adder_2_out, not_2_out;

  assign not_1_out = ~in_1;  // NOT_Gate not_1, 3 bits wide
  Adder #(.width(3)) adder_1 (.a(not_1_out), .b(3'b001), .out(adder_1_out));  // open: cin, cout
  Multiplexer #(.width(8)) multiplexer_1 (
    .in0({{5{1'b0}}, in_1}), .in1(adder_2_out), .out(out_2), .sel(in_1[2]));  // open: en
  assign not_2_out = ~{{5{1'b0}}, adder_1_out};  // NOT_Gate not_2, 8 bits wide
  Adder adder_2 (.a(not_2_out), .b(8'h1), .out(adder_2_out));  // open: cin, cout
endmodule

module is_hit_bat (
  input  [7:0] BallY,
  input  [4:0] Bat,
  output hits_star
);

  wire comparator_1_eq, comparator_2_eq, comparator_3_eq;
  wire [4:0] adder_1_out, adder_2_out, bit_extender_1_out;
  wire [7:0] shifter_1_out;

  Shifter #(.shift("lr")) shifter_1 (.in(BallY), .\dist (3'b011), .out(shifter_1_out));
  Bit_Extender #(.out_width(5)) bit_extender_1 (.in(shifter_1_out), .out(bit_extender_1_out));
  Adder #(.width(5)) adder_1 (.a(Bat), .b(5'b00001), .out(adder_1_out));  // open: cin, cout
  Adder #(.width(5)) adder_2 (.a(Bat), .b(5'b00010), .out(adder_2_out));  // open: cin, cout
  Comparator #(.width(5), .mode("unsigned")) comparator_1 (
    .a(bit_extender_1_out), .b(Bat), .eq(comparator_1_eq));  // open: gt, lt
  Comparator #(.width(5), .mode("unsigned")) comparator_2 (
    .a(bit_extender_1_out), .b(adder_1_out), .eq(comparator_2_eq));  // open: gt, lt
  Comparator #(.width(5), .mode("unsigned")) comparator_3 (
    .a(bit_extender_1_out), .b(adder_2_out), .eq(comparator_3_eq));  // open: gt, lt
  or or_1 (hits_star, comparator_1_eq, comparator_2_eq, comparator_3_eq);
endmodule

module invert_V (
  input  [7:0] in_1,
  output [7:0] out_2
);

  wire comparator_1_eq;
  wire [7:0] adder_1_out, not_1_out;

  assign not_1_out = ~in_1;  // NOT_Gate not_1, 8 bits wide
  Comparator comparator_1 (.a(in_1), .b(8'hfc), .eq(comparator_1_eq));  // open: gt, lt
  Adder adder_1 (.a(not_1_out), .b(8'h1), .out(adder_1_out));  // open: cin, cout
  Multiplexer #(.width(8)) multiplexer_1 (
    .in0(adder_1_out), .in1(8'h3), .out(out_2), .sel(comparator_1_eq));  // open: en
endmodule

module _8_to_3 (
  input  [7:0] in_1,
  output [2:0] out_2
);

  wire [2:0] adder_2_out, bit_extender_1_out, bit_extender_2_out, not_2_out;
  wire [7:0] adder_1_out, not_1_out;

  assign not_1_out = ~in_1;  // NOT_Gate not_1, 8 bits wide
  Bit_Extender #(.out_width(3)) bit_extender_1 (.in(in_1), .out(bit_extender_1_out));
  Adder adder_1 (.a(not_1_out), .b(8'h1), .out(adder_1_out));  // open: cin, cout
  Multiplexer #(.width(3)) multiplexer_1 (
    .in0(bit_extender_1_out), .in1(adder_2_out), .out(out_2), .sel(in_1[7]));  // open: en
  assign not_2_out = ~bit_extender_2_out;  // NOT_Gate not_2, 3 bits wide
  Bit_Extender #(.out_width(3)) bit_extender_2 (.in(adder_1_out), .out(bit_extender_2_out));
  Adder #(.width(3)) adder_2 (.a(not_2_out), .b(3'b001), .out(adder_2_out));  // open: cin, cout
endmodule

module Input_Output (
  input  [7:0] in_1,
  input  block,
  input  [7:0] INPUT_BallX_8b,
  input  res,
  input  [7:0] INPUT_BallY_8b,
  input  run,
  output [7:0] out_7
);

  wire and_1_out, and_2_out, and_3_out, and_4_out, and_5_out, and_6_out, block_t, cdm_8_mark5_1_p1,
       cdm_8_mark5_1_p2, cdm_8_mark5_1_p4, cdm_8_mark5_1_p5, cdm_8_mark5_1_p6, cdm_8_mark5_1_p7,
       cdm_8_mark5_1_p8, clock, code, data, decoder_1_out0, decoder_1_out1, decoder_1_out3, decoder_1_out4,
       decoder_1_out5, decoder_1_out8, I_Osel, in_out_prime, mem, nand_1_out, nor_1_out, not_1_out,
       not_2_out, not_3_out, not_4_out, not_5_out, not_6_out, RAM;
  wire [3:0] I_Oadr;
  wire [7:0] cdm_8_mark5_1_p12, cdm_8_mark5_1_p13, divider_1_out, I_Odat, register_1_q, register_2_q;
  wire [7:4] cdm_8_mark5_1_p11;

  Decoder #(.select(4), .enable("false")) decoder_1 (
    .out0(decoder_1_out0), .out1(decoder_1_out1), .out3(decoder_1_out3), .out4(decoder_1_out4),
    .out5(decoder_1_out5), .out8(decoder_1_out8), .sel(I_Oadr));  // open: out2, out6, out7, out9, out10, out11, out12, out13, out14, out15
  and and_1 (and_1_out, decoder_1_out0, I_Osel, ~in_out_prime);  // AND_Gate
  and and_2 (and_2_out, decoder_1_out1, in_out_prime, I_Osel);
  Register #(.trigger("high")) register_1 (.D(I_Odat), .Q(register_1_q), .clk(and_1_out));  // open: en, clr
  assign I_Odat = and_2_out ? divider_1_out : 8'bz;  // Controlled_Buffer controlled_buffer_1
  Divider divider_1 (.a(register_1_q), .b(8'h3), .out(divider_1_out));  // open: upper, rem
  not not_1 (not_1_out, in_out_prime);
  LED led_1 (.in(and_3_out));
  and and_3 (and_3_out, not_1_out, I_Osel, decoder_1_out8);
  LED led_2 (.in(and_3_out));
  LED led_3 (.in(and_4_out));
  and and_4 (and_4_out, in_out_prime, I_Osel, decoder_1_out3);
  and and_5 (and_5_out, in_out_prime, I_Osel, decoder_1_out4);
  LED led_4 (.in(and_5_out));
  and and_6 (and_6_out, in_out_prime, I_Osel, decoder_1_out5);
  LED led_5 (.in(and_6_out));
  assign I_Odat = and_4_out ? register_2_q : 8'bz;  // Controlled_Buffer controlled_buffer_2
  assign I_Odat = and_5_out ? INPUT_BallX_8b : 8'bz;  // Controlled_Buffer controlled_buffer_3
  assign I_Odat = and_6_out ? INPUT_BallY_8b : 8'bz;  // Controlled_Buffer controlled_buffer_4
  nor nor_1 (nor_1_out, and_2_out, and_1_out, and_3_out, and_4_out, and_5_out, and_6_out);
  not not_2 (not_2_out, block_t);
  Register register_2 (.D(in_1), .en(not_3_out), .Q(register_2_q), .clk(clock), .clr(block_t));
  not not_3 (not_3_out, block_t);
  and and_7 (RAM, nor_1_out, data);
  Register register_3 (.D(I_Odat), .en(not_2_out), .Q(out_7), .clk(and_3_out));  // open: clr
  // Probe on I_Oadr
  // Probe on I_Odat
  Clock clock_1 (.out(clock));
  and and_8 (I_Osel, not_4_out, clock, data);
  or or_1 (block_t, block, res, run);
  // Probe on nothing
  // Probe on cdm_8_mark5_1_p5
  // Probe on cdm_8_mark5_1_p4
  // Probe on cdm_8_mark5_1_p2
  // Probe on cdm_8_mark5_1_p1
  not not_4 (not_4_out, nand_1_out);
  // Probe on cdm_8_mark5_1_p6
  // Probe on cdm_8_mark5_1_p7
  // CdM_8_mark5 cdm_8_mark5_1: pin names not known; wires that end beside it: cdm_8_mark5_1_p1, cdm_8_mark5_1_p2, clock, cdm_8_mark5_1_p4, cdm_8_mark5_1_p5, cdm_8_mark5_1_p6, cdm_8_mark5_1_p7, cdm_8_mark5_1_p8, mem, in_out_prime, {cdm_8_mark5_1_p11, I_Oadr}, cdm_8_mark5_1_p12, cdm_8_mark5_1_p13
  nand nand_1 (nand_1_out, cdm_8_mark5_1_p11[4], cdm_8_mark5_1_p11[5], cdm_8_mark5_1_p11[6], cdm_8_mark5_1_p11[7]);
  Decoder #(.disabled(0)) decoder_2 (.out0(code), .out1(data), .sel(cdm_8_mark5_1_p8), .en(mem));
  assign I_Odat = not_5_out ? cdm_8_mark5_1_p12 : 8'bz;  // Controlled_Buffer controlled_buffer_5
  not not_5 (not_5_out, in_out_prime);
  assign cdm_8_mark5_1_p13 = in_out_prime ? I_Odat : 8'bz;  // Controlled_Buffer controlled_buffer_6
  not not_6 (not_6_out, in_out_prime);
  Pull_Resistor pull_resistor_1 (.node(I_Oadr[0]));
  Pull_Resistor pull_resistor_2 (.node(I_Oadr[1]));
  Pull_Resistor pull_resistor_3 (.node(I_Oadr[2]));
  Pull_Resistor pull_resistor_4 (.node(I_Oadr[3]));
  Pull_Resistor pull_resistor_5 (.node(cdm_8_mark5_1_p11[4]));
  Pull_Resistor pull_resistor_6 (.node(cdm_8_mark5_1_p11[5]));
  Pull_Resistor pull_resistor_7 (.node(cdm_8_mark5_1_p11[6]));
  Pull_Resistor pull_resistor_8 (.node(cdm_8_mark5_1_p11[7]));
  ROM rom_1 (.addr({cdm_8_mark5_1_p11, I_Oadr}), .data(I_Odat), .sel(code));
  RAM #(.bus("separate")) ram_1 (
    .addr({cdm_8_mark5_1_p11, I_Oadr}), .din(I_Odat), .data(I_Odat), .str(not_6_out), .sel(RAM), .clk(clock),
    .ld(in_out_prime), .clr(res));

  // Other names for the same wires on the sheet: rd_wr_prime = in_out_prime; resey = res

  // Notes on the sheet:
  //   0xf0
  //   0xf1
  //   (because proramm can't divide fast)
  //   in case vx = | 3 |
  //   IO 0xf8
  //   IO 0xf3
  //   IO 0xf4
  //   IO 0xf5
  //   OUTPUT 0xf8 addr
  //   INPUT Vxy (0b00yyyxxx)
  //   RightBat Y
  //   *to controller
  //   I/O BUS
  //   4 lower bit adr
  //   "robot_release.asm"
  //   INSTR
  //   contents of rom_1 (hex, n*v repeats v):
  //   d0 f3 b0 d2 f5 ba d1 f4 b5 0 e1 11 d0 f8 a2 ee 0 d3 4 43 f ed 1c d0 f8 a2 ee 0 85 d3 e4 1d c0 d3 7
  //   4c 84 d3 fd 7c e1 32 d0 f0 a1 d1 f1 b5 ee 3b d3 fe 7c e1 3b 91 d3 7f 4d c4 d3 20 73 ea 7f 98 98 98
  //   d3 3 73 e1 5c d0 ff a2 6 d0 0 d3 0 15 23 d0 0 19 23 d0 ff b2 ee 6b d3 2 73 e1 69 d3 0 d0 0 15 23 ee
  //   6b d3 0 d0 0 16 23 d0 1 43 f e1 77 ee 78 86 d0 f8 a2 ee 0 ee c1 98 98 98 d3 f8 5c d3 fd 73 e1 9e d0
  //   ff a2 6 d3 0 d0 0 19 23 d0 0 19 23 d0 ff b2 85 ee af d3 fe 73 e1 ac d3 0 d0 0 15 23 85 ee af d3 0 85
  //   d0 0 16 23 d0 1 43 f e1 bc 86 ee bc d0 f8 a2 ee 0 d4
  //   DATA
endmodule

module switch (
  input  tap_here_x2,
  output out_2
);

  Counter #(.width(1), .max('h1)) counter_1 (
    .D(tap_here_x2), .Q(out_2), .clk(tap_here_x2));  // open: load, count, carry, clr

  // Notes on the sheet:
  //   ^
  //   |
  //   and again
endmodule

module Level (
  input  res,
  input  set,
  input  [4:0] in_3,
  output no_start,
  output hard,
  output norm,
  output ez
);

  wire clock_1_out, not_1_out;
  wire [4:0] register_2_q;

  Register #(.width(1), .trigger("high")) register_1 (.D(1'b1), .Q(no_start), .clk(set), .clr(res));  // open: en
  not not_1 (not_1_out, no_start);
  Register #(.width(5), .trigger("high")) register_2 (
    .D(in_3), .en(not_1_out), .Q(register_2_q), .clk(clock_1_out));  // open: clr
  Clock clock_1 (.out(clock_1_out));
  Comparator #(.width(5), .mode("unsigned")) comparator_1 (.a(register_2_q), .b(5'b10100), .gt(hard));  // open: eq, lt
  Comparator #(.width(5), .mode("unsigned")) comparator_2 (.a(register_2_q), .b(5'b01001), .lt(ez));  // open: gt, eq
  nor nor_1 (norm, hard, ez);

  // Notes on the sheet:
  //   aka menu
endmodule

module Joystick (
  input  [4:0] in_1,
  output [4:0] out_2
);

  wire and_1_out, and_2_out, clock_1_out, comparator_1_eq, comparator_2_gt, comparator_3_lt, not_1_out,
       not_2_out, not_3_out;
  wire [4:0] register_2_q;

  Clock clock_1 (.out(clock_1_out));
  Register #(.width(5)) register_1 (.D(in_1), .en(not_2_out), .Q(out_2), .clk(clock_1_out));  // open: clr
  not not_1 (not_1_out, clock_1_out);
  not not_2 (not_2_out, and_2_out);
  Register #(.width(5)) register_2 (.D(out_2), .Q(register_2_q), .clk(not_1_out));  // open: en, clr
  Comparator #(.width(5), .mode("unsigned")) comparator_1 (
    .a(in_1), .b(5'b10000), .eq(comparator_1_eq));  // open: gt, lt
  Comparator #(.width(5), .mode("unsigned")) comparator_2 (
    .a(register_2_q), .b(5'b01101), .gt(comparator_2_gt));  // open: eq, lt
  Comparator #(.width(5), .mode("unsigned")) comparator_3 (
    .a(register_2_q), .b(5'b10011), .lt(comparator_3_lt));  // open: gt, eq
  and and_1 (and_1_out, comparator_2_gt, comparator_3_lt);
  and and_2 (and_2_out, comparator_1_eq, not_3_out);
  not not_3 (not_3_out, and_1_out);

  // Notes on the sheet:
  //   This circuit fixates left bat when player suddenly lets go the joysyick
endmodule

module Menu_graphics (
  input  [4:0] chip_id,
  input  [2:0] level,
  output [31:0] out_3
);

  wire and_1_out, and_2_out, and_3_out, and_4_out, and_5_out, and_6_out, and_7_out, decoder_1_out3,
       decoder_1_out4, decoder_1_out5, decoder_1_out6, decoder_1_out7, decoder_1_out8, decoder_1_out9,
       decoder_1_out10, decoder_1_out11, decoder_1_out12, decoder_1_out13, decoder_1_out14, decoder_1_out15,
       decoder_1_out16, decoder_1_out18, decoder_1_out19, decoder_1_out20, decoder_1_out21, decoder_1_out22,
       mark;
  wire [31:0] controlled_buffer_1_out, controlled_buffer_21_out;

  Decoder #(.select(5), .enable("false")) decoder_1 (
    .out1(mark), .out3(decoder_1_out3), .out4(decoder_1_out4), .out5(decoder_1_out5), .out6(decoder_1_out6),
    .out7(decoder_1_out7), .out8(decoder_1_out8), .out9(decoder_1_out9), .out10(decoder_1_out10),
    .out11(decoder_1_out11), .out12(decoder_1_out12), .out13(decoder_1_out13), .out14(decoder_1_out14),
    .out15(decoder_1_out15), .out16(decoder_1_out16), .out18(decoder_1_out18), .out19(decoder_1_out19),
    .out20(decoder_1_out20), .out21(decoder_1_out21), .out22(decoder_1_out22), .sel(chip_id));  // open: out0, out2, out17, out23, out24, out25, out26, out27, out28, out29, out30, out31
  and and_1 (and_1_out, ~decoder_1_out3, ~decoder_1_out4, ~decoder_1_out5, ~decoder_1_out6, ~decoder_1_out7, ~decoder_1_out8);  // AND_Gate
  assign controlled_buffer_1_out = decoder_1_out7 ? {32{1'b0}} : 32'bz;  // Controlled_Buffer controlled_buffer_1
  assign controlled_buffer_1_out = decoder_1_out6 ? 32'hfbea800 : 32'bz;  // Controlled_Buffer controlled_buffer_2
  assign controlled_buffer_1_out = decoder_1_out5 ? 32'h208a800 : 32'bz;  // Controlled_Buffer controlled_buffer_3
  assign controlled_buffer_1_out = decoder_1_out4 ? 32'h210a800 : 32'bz;  // Controlled_Buffer controlled_buffer_4
  assign controlled_buffer_1_out = decoder_1_out3 ? 32'hfbef800 : 32'bz;  // Controlled_Buffer controlled_buffer_5
  assign controlled_buffer_1_out = decoder_1_out15 ? 32'ha28a800 : 32'bz;  // Controlled_Buffer controlled_buffer_6
  assign controlled_buffer_1_out = decoder_1_out14 ? 32'ha28a800 : 32'bz;  // Controlled_Buffer controlled_buffer_7
  assign controlled_buffer_1_out = decoder_1_out13 ? 32'hfbee800 : 32'bz;  // Controlled_Buffer controlled_buffer_8
  assign controlled_buffer_1_out = decoder_1_out12 ? {32{1'b0}} : 32'bz;  // Controlled_Buffer controlled_buffer_9
  assign controlled_buffer_1_out = decoder_1_out11 ? 32'h7be7800 : 32'bz;  // Controlled_Buffer controlled_buffer_10
  assign controlled_buffer_1_out = decoder_1_out10 ? 32'ha22a000 : 32'bz;  // Controlled_Buffer controlled_buffer_11
  assign controlled_buffer_1_out = decoder_1_out9 ? 32'ha22a000 : 32'bz;  // Controlled_Buffer controlled_buffer_12
  assign controlled_buffer_1_out = decoder_1_out8 ? 32'h7be7800 : 32'bz;  // Controlled_Buffer controlled_buffer_13
  assign controlled_buffer_1_out = decoder_1_out22 ? 32'h3e0000 : 32'bz;  // Controlled_Buffer controlled_buffer_14
  assign controlled_buffer_1_out = decoder_1_out21 ? 32'h7100000 : 32'bz;  // Controlled_Buffer controlled_buffer_15
  assign controlled_buffer_1_out = decoder_1_out20 ? 32'h888f800 : 32'bz;  // Controlled_Buffer controlled_buffer_16
  assign controlled_buffer_1_out = decoder_1_out19 ? 32'h8902800 : 32'bz;  // Controlled_Buffer controlled_buffer_17
  assign controlled_buffer_1_out = decoder_1_out18 ? 32'hfbee800 : 32'bz;  // Controlled_Buffer controlled_buffer_18
  assign controlled_buffer_1_out = decoder_1_out16 ? 32'hdb6b800 : 32'bz;  // Controlled_Buffer controlled_buffer_19
  and and_2 (and_2_out, ~decoder_1_out9, ~decoder_1_out10, ~decoder_1_out11, ~decoder_1_out12, ~decoder_1_out13, ~decoder_1_out14, ~decoder_1_out15, ~decoder_1_out16, ~decoder_1_out18, ~decoder_1_out19, ~decoder_1_out20, ~decoder_1_out21, ~decoder_1_out22);  // AND_Gate
  and and_3 (and_3_out, and_1_out, and_2_out);
  assign controlled_buffer_1_out = and_3_out ? {32{1'b0}} : 32'bz;  // Controlled_Buffer controlled_buffer_20
  and and_4 (and_4_out, mark, level[0]);
  assign controlled_buffer_21_out = and_4_out ? 32'h1000000 : 32'bz;  // Controlled_Buffer controlled_buffer_21
  and and_5 (and_5_out, level[1], mark);
  assign controlled_buffer_21_out = and_5_out ? 32'h80000 : 32'bz;  // Controlled_Buffer controlled_buffer_22
  and and_6 (and_6_out, level[2], mark);
  assign out_3 = controlled_buffer_1_out | controlled_buffer_21_out;  // OR_Gate or_1, 32 bits wide
  assign controlled_buffer_21_out = and_7_out ? {32{1'b0}} : 32'bz;  // Controlled_Buffer controlled_buffer_23
  and and_7 (and_7_out, ~and_4_out, ~and_5_out, ~and_6_out);  // AND_Gate
  assign controlled_buffer_21_out = and_6_out ? 32'h2000 : 32'bz;  // Controlled_Buffer controlled_buffer_24

  // Other names for the same wires on the sheet: level_mark[2:0] = level
endmodule

module Difficulty_mechanics (
  input  [7:0] ball_X,
  input  [2:0] level,
  input  [7:0] right_bat,
  input  [7:0] VX,
  output [2:0] VY,
  output [2:0] VX_2,
  output [7:0] right_bat_fin
);

  wire and_1_out, and_2_out, and_3_out, and_4_out, and_5_out, clock_1_out, comparator_1_gt, comparator_2_lt,
       comparator_3_lt, comparator_4_gt, decoder_1_out0, decoder_1_out1, decoder_1_out2, decoder_1_out3,
       decoder_1_out4, decoder_1_out5, decoder_1_out6, decoder_1_out7, decoder_1_out8, decoder_1_out9, miss,
       not_1_out, or_1_out, or_2_out, or_3_out, P, reset, sign, \time ;
  wire [2:0] controlled_inverter_1_out;
  wire [3:0] random_1_out;
  wire [4:0] divider_1_rem;
  wire [7:0] adder_2_out, multiplexer_1_out;

  assign VY = level[0] ? 3'b011 : 3'bz;  // Controlled_Buffer controlled_buffer_1
  Comparator #(.mode("unsigned")) comparator_1 (.a(right_bat), .b(8'h12), .gt(comparator_1_gt));  // open: eq, lt
  Comparator #(.mode("unsigned")) comparator_2 (.a(right_bat), .b(8'hef), .lt(comparator_2_lt));  // open: gt, eq
  // Probe on ball_X
  assign VY = level[1] ? 3'b010 : 3'bz;  // Controlled_Buffer controlled_buffer_2
  assign VY = level[2] ? 3'b001 : 3'bz;  // Controlled_Buffer controlled_buffer_3
  assign controlled_inverter_1_out = level[1] ? ~VY : 3'bz;  // Controlled_Inverter controlled_inverter_1
  assign controlled_inverter_1_out = level[2] ? ~3'b011 : 3'bz;  // Controlled_Inverter controlled_inverter_2
  and and_1 (and_1_out, comparator_1_gt, sign);
  and and_2 (and_2_out, ~sign, ~comparator_2_lt);  // AND_Gate
  Comparator #(.mode("unsigned")) comparator_3 (.a(ball_X), .b(8'h50), .gt(P), .lt(comparator_3_lt));  // open: eq
  or or_1 (or_1_out, comparator_3_lt, comparator_4_gt);
  Comparator #(.mode("unsigned")) comparator_4 (.a(ball_X), .b(8'h9f), .gt(comparator_4_gt));  // open: eq, lt
  nor nor_1 (reset, level[2], level[1], level[0]);
  assign VY = reset ? 3'b000 : 3'bz;  // Controlled_Buffer controlled_buffer_4
  assign controlled_inverter_1_out = level[0] ? ~3'b001 : 3'bz;  // Controlled_Inverter controlled_inverter_3
  Adder #(.width(3)) adder_1 (.a(controlled_inverter_1_out), .b(3'b001), .out(VX_2));  // open: cin, cout
  Clock clock_1 (.out(clock_1_out));
  not not_1 (not_1_out, or_1_out);
  assign VX_2 = reset ? 3'b000 : 3'bz;  // Controlled_Buffer controlled_buffer_5
  or or_2 (or_2_out, and_1_out, and_2_out);
  S_R_Flip_Flop s_r_ff_1 (.S(not_1_out), .clk(clock_1_out), .R(or_1_out), .Q(\time ));  // open: Qn, preset, reset, en
  // Probe on {sign, random_1_out}
  Random #(.width(5), .seed(833264259)) random_1 (.clk(P), .out({sign, random_1_out}));  // open: next, clr
  Divider #(.width(5)) divider_1 (.a({sign, random_1_out}), .b(5'b01010), .rem(divider_1_rem));  // open: out, upper
  Multiplexer #(.width(8), .enable("false")) multiplexer_1 (
    .in0(8'h16), .in1(8'hf0), .out(multiplexer_1_out), .sel(or_2_out));
  // Probe on right_bat
  Decoder #(.select(5), .enable("false")) decoder_1 (
    .out0(decoder_1_out0), .out1(decoder_1_out1), .out2(decoder_1_out2), .out3(decoder_1_out3),
    .out4(decoder_1_out4), .out5(decoder_1_out5), .out6(decoder_1_out6), .out7(decoder_1_out7),
    .out8(decoder_1_out8), .out9(decoder_1_out9), .sel(divider_1_rem));  // open: out10, out11, out12, out13, out14, out15, out16, out17, out18, out19, out20, out21, out22, out23, out24, out25, out26, out27, out28, out29, out30, out31
  Adder adder_2 (.a(multiplexer_1_out), .b(right_bat), .out(adder_2_out));  // open: cin, cout
  or or_3 (or_3_out, decoder_1_out2, decoder_1_out8, decoder_1_out9, decoder_1_out6);
  Multiplexer #(.width(8), .enable("false")) multiplexer_2 (
    .in0(right_bat), .in1(adder_2_out), .out(right_bat_fin), .sel(and_3_out));
  and and_3 (and_3_out, ~VX[2], miss, \time );  // AND_Gate
  and and_4 (and_4_out, or_3_out, level[2]);
  and and_5 (and_5_out, level[1], decoder_1_out1);
  // Probe on right_bat_fin
  or or_4 (miss, and_4_out, and_5_out);

  // Other names for the same wires on the sheet: hard = level[0]; normal = level[1]; easy = level[2]

  // Notes on the sheet:
  //   hard -> vx|vy = 1|3 missing P = 0
  //   normal -> vx|vy = 2|2 missing P in time ~ 1/10
  //   easy -> vx|vy = 3|1 missing P in time ~ 4/10
  //   when ball goes left -> no misses
  //   9
  //   random() % 10
  //   switch bat with -16/16
  //   right bat to miss
endmodule
